// Logisim project cpuA.circ as structural Verilog: 1 circuit, main circuit main
module main (
  input  [7:0] in_1,
  input  mwr,
  input  mclk,
  input  in_4,
  input  in_5,
  input  in_6,
  input  in_7,
  input  in_8,
  input  in_9,
  input  rwrclk,
  input  selres,
  input  clr,
  input  [7:0] idbus
);

  wire and_1_out, and_2_out, and_3_out, and_4_out, and_5_out, and_6_out, and_7_out, and_8_out,
       decoder_1_out0, decoder_1_out1, decoder_1_out2, decoder_1_out3, not_1_out, not_2_out;
  wire [7:0] adder_1_out, adr_q, controlled_buffer_1_out, controlled_buffer_5_out, controlled_buffer_8_out,
       opA_q, opB_q, ram_1_data, res_q;

  Decoder #(.select(2)) decoder_1 (
    .out0(decoder_1_out0), .out1(decoder_1_out1), .out2(decoder_1_out2), .out3(decoder_1_out3),
    .sel({in_4, in_5}));  // open: en
  assign controlled_buffer_1_out = decoder_1_out3 ? idbus : 8'bz;  // Controlled_Buffer controlled_buffer_1
  assign controlled_buffer_1_out = decoder_1_out0 ? controlled_buffer_5_out : 8'bz;  // Controlled_Buffer controlled_buffer_2
  assign controlled_buffer_1_out = decoder_1_out1 ? ram_1_data : 8'bz;  // Controlled_Buffer controlled_buffer_3
  assign controlled_buffer_1_out = decoder_1_out2 ? in_1 : 8'bz;  // Controlled_Buffer controlled_buffer_4
  Register adr (.D(controlled_buffer_1_out), .en(and_1_out), .Q(adr_q), .clk(rwrclk), .clr(clr));
  and and_1 (and_1_out, ~in_6, ~in_7);  // AND_Gate
  assign controlled_buffer_5_out = and_2_out ? adr_q : 8'bz;  // Controlled_Buffer controlled_buffer_5
  and and_2 (and_2_out, ~in_8, ~in_9);  // AND_Gate
  RAM #(.bus("separate")) ram_1 (
    .addr(adr_q), .din(controlled_buffer_5_out), .data(ram_1_data), .str(mwr), .clk(mclk), .ld(not_1_out),
    .clr(clr));  // open: sel
  not not_1 (not_1_out, mwr);
  Register opA (.D(controlled_buffer_1_out), .en(and_4_out), .Q(opA_q), .clk(rwrclk), .clr(clr));
  and and_3 (and_3_out, ~in_8, in_9);  // AND_Gate
  and and_4 (and_4_out, ~in_6, in_7);  // AND_Gate
  assign controlled_buffer_5_out = and_3_out ? opA_q : 8'bz;  // Controlled_Buffer controlled_buffer_6
  and and_5 (and_5_out, in_6, ~in_7);  // AND_Gate
  assign controlled_buffer_5_out = and_6_out ? opB_q : 8'bz;  // Controlled_Buffer controlled_buffer_7
  Register opB (.D(controlled_buffer_1_out), .en(and_5_out), .Q(opB_q), .clk(rwrclk), .clr(clr));
  and and_6 (and_6_out, in_8, ~in_9);  // AND_Gate
  Adder adder_1 (.a(opA_q), .b(opB_q), .out(adder_1_out));  // open: cin, cout
  not not_2 (not_2_out, selres);
  assign controlled_buffer_8_out = not_2_out ? adder_1_out : 8'bz;  // Controlled_Buffer controlled_buffer_8
  assign controlled_buffer_8_out = selres ? controlled_buffer_1_out : 8'bz;  // Controlled_Buffer controlled_buffer_9
  and and_7 (and_7_out, in_6, in_7);
  assign controlled_buffer_5_out = and_8_out ? res_q : 8'bz;  // Controlled_Buffer controlled_buffer_10
  Register res (.D(controlled_buffer_8_out), .en(and_7_out), .Q(res_q), .clk(rwrclk), .clr(clr));
  and and_8 (and_8_out, in_8, in_9);

  // Notes on the sheet:
  //   dbsel
  //   rwrsel
  //   rrdsel
endmodule
