// Logisim project cpuC.circ as structural Verilog: 1 circuit, main circuit main
module main (
  input  [7:0] user_input,
  input  mempersist,
  input  [3:0] instr,
  input  [3:0] sw0,
  input  manual,
  input  reset,
  input  [3:0] in_7,
  input  [3:0] in_8,
  input  [3:0] in_9,
  input  [3:0] in_10,
  input  manual_2
);

  wire and_1_out, and_2_out, and_3_out, and_4_out, and_5_out, button_1_out, button_2_out, clock_1_out,
       decoder_1_out0, decoder_1_out1, decoder_1_out2, decoder_1_out3, decoder_2_out0, decoder_2_out1,
       decoder_2_out2, decoder_2_out3, decoder_3_out0, decoder_3_out1, decoder_3_out2, decoder_3_out3,
       decoder_4_out0, decoder_4_out1, decoder_4_out2, decoder_4_out3, decoder_5_out0, decoder_5_out1,
       decoder_5_out2, decoder_5_out3, decoder_6_out0, decoder_6_out1, decoder_6_out2, decoder_6_out3,
       decoder_7_out0, decoder_7_out1, decoder_7_out2, decoder_7_out3, decoder_8_out0, decoder_8_out1,
       decoder_8_out2, decoder_8_out3, decoder_9_out0, decoder_9_out1, not_1_out, not_2_out, not_3_out,
       not_4_out, not_5_out, not_6_out, or_1_out, or_2_out, or_3_out, or_4_out, or_5_out,
       pull_resistor_23_node, pull_resistor_24_node;
  wire [1:0] controlled_buffer_28_out_2, pull_resistor_1_node, pull_resistor_2_node, pull_resistor_11_node,
       pull_resistor_12_node;
  wire [3:0] controlled_buffer_2_out, controlled_buffer_2_out_2, controlled_buffer_6_out,
       controlled_buffer_28_out_3, controlled_buffer_28_out_4, controlled_buffer_33_out,
       controlled_buffer_33_out_2, pull_resistor_6_node, pull_resistor_9_node, pull_resistor_10_node,
       pull_resistor_10_node_2, pull_resistor_14_node, pull_resistor_16_node;
  wire [7:0] A0_q, adder_1_out, controlled_buffer_1_out, controlled_buffer_9_out, counter_1_q, D0_q, D1_q,
       OC_q, PC_q, pull_resistor_19_node, pull_resistor_21_node, R0_q, ram_1_data, register_2_q, rom_1_data,
       subtractor_1_out;
  wire [7:4] pull_resistor_9_node_2;
  wire [15:0] register_1_q, rom_2_data;
  wire [15:8] controlled_buffer_28_out;

  Hex_Digit_Display hex_digit_display_1 (.value(controlled_buffer_2_out_2));  // open: dp
  Hex_Digit_Display hex_digit_display_2 (.value(controlled_buffer_2_out));  // open: dp
  Hex_Digit_Display hex_digit_display_3 (.value(pull_resistor_10_node_2));  // open: dp
  Hex_Digit_Display hex_digit_display_4 (.value(pull_resistor_10_node_2));  // open: dp
  Hex_Digit_Display hex_digit_display_5 (.value(pull_resistor_10_node));  // open: dp
  Hex_Digit_Display hex_digit_display_6 (.value(pull_resistor_9_node_2));  // open: dp
  Hex_Digit_Display hex_digit_display_7 (.value(pull_resistor_9_node));  // open: dp
  Decoder #(.select(2), .disabled(0)) decoder_1 (
    .out0(decoder_1_out0), .out1(decoder_1_out1), .out2(decoder_1_out2), .out3(decoder_1_out3),
    .sel(pull_resistor_2_node), .en(or_4_out));
  Decoder #(.select(2), .disabled(0)) decoder_2 (
    .out0(decoder_2_out0), .out1(decoder_2_out1), .out2(decoder_2_out2), .out3(decoder_2_out3),
    .sel(pull_resistor_1_node), .en(or_2_out));
  Pull_Resistor pull_resistor_1 (.node(pull_resistor_1_node));
  Pull_Resistor pull_resistor_2 (.node(pull_resistor_2_node));
  Decoder #(.select(2)) decoder_3 (
    .out0(decoder_3_out0), .out1(decoder_3_out1), .out2(decoder_3_out2), .out3(decoder_3_out3),
    .sel(controlled_buffer_28_out_2));  // open: en
  Pull_Resistor #(.pull(1)) pull_resistor_3 (.node(pull_resistor_6_node[2]));
  Pull_Resistor #(.pull(1)) pull_resistor_4 (.node(pull_resistor_6_node[3]));
  Pull_Resistor pull_resistor_5 (.node(pull_resistor_6_node[1]));
  Pull_Resistor #(.pull(1)) pull_resistor_6 (.node(pull_resistor_6_node[0]));
  Pull_Resistor pull_resistor_7 (.node(pull_resistor_16_node[3]));
  Pull_Resistor pull_resistor_8 (.node(pull_resistor_16_node[2]));
  Hex_Digit_Display hex_digit_display_8 (.value(pull_resistor_10_node));  // open: dp
  Decoder #(.select(2), .disabled(0)) decoder_4 (
    .out0(decoder_4_out0), .out1(decoder_4_out1), .out2(decoder_4_out2), .out3(decoder_4_out3),
    .sel(pull_resistor_12_node), .en(or_1_out));
  Pull_Resistor pull_resistor_9 (.node({pull_resistor_9_node_2, pull_resistor_9_node}));
  Pull_Resistor pull_resistor_10 (.node({pull_resistor_10_node_2, pull_resistor_10_node}));
  Decoder #(.select(2), .disabled(0)) decoder_5 (
    .out0(decoder_5_out0), .out1(decoder_5_out1), .out2(decoder_5_out2), .out3(decoder_5_out3),
    .sel(pull_resistor_11_node), .en(or_3_out));
  Pull_Resistor pull_resistor_11 (.node(pull_resistor_11_node));
  Pull_Resistor pull_resistor_12 (.node(pull_resistor_12_node));
  Pull_Resistor pull_resistor_13 (.node(pull_resistor_16_node[1]));
  Pull_Resistor pull_resistor_14 (.node(pull_resistor_14_node[0]));
  Pull_Resistor pull_resistor_15 (.node(pull_resistor_14_node[2]));
  Pull_Resistor pull_resistor_16 (.node(pull_resistor_16_node[0]));
  Pull_Resistor pull_resistor_17 (.node(pull_resistor_14_node[1]));
  Pull_Resistor pull_resistor_18 (.node(pull_resistor_14_node[3]));
  assign controlled_buffer_1_out = decoder_4_out3 ? {pull_resistor_10_node_2, pull_resistor_10_node} : 8'bz;  // Controlled_Buffer controlled_buffer_1
  Hex_Digit_Display hex_digit_display_9 (.value(controlled_buffer_33_out_2));  // open: dp
  assign {controlled_buffer_2_out_2, controlled_buffer_2_out} = decoder_9_out0 ? A0_q : 8'bz;  // Controlled_Buffer controlled_buffer_2
  assign controlled_buffer_1_out = decoder_4_out2 ? A0_q : 8'bz;  // Controlled_Buffer controlled_buffer_3
  Register A0 (
    .D(controlled_buffer_1_out), .en(decoder_5_out0), .Q(A0_q), .clk(controlled_buffer_28_out[12]),
    .clr(or_5_out));
  assign {pull_resistor_9_node_2, pull_resistor_9_node} = decoder_2_out0 ? A0_q : 8'bz;  // Controlled_Buffer controlled_buffer_4
  assign {pull_resistor_10_node_2, pull_resistor_10_node} = decoder_1_out0 ? A0_q : 8'bz;  // Controlled_Buffer controlled_buffer_5
  Decoder #(.select(2)) decoder_6 (
    .out0(decoder_6_out0), .out1(decoder_6_out1), .out2(decoder_6_out2), .out3(decoder_6_out3),
    .sel(controlled_buffer_28_out_3[1:0]));  // open: en
  DotMatrix #(.inputtype("row"), .matrixcols(4), .matrixrows(1)) dotmatrix_1 (.row0(controlled_buffer_33_out));
  assign controlled_buffer_6_out = decoder_3_out2 ? pull_resistor_16_node : 4'bz;  // Controlled_Buffer controlled_buffer_6
  assign controlled_buffer_6_out = decoder_3_out3 ? pull_resistor_14_node : 4'bz;  // Controlled_Buffer controlled_buffer_7
  ROM #(.addrWidth(4)) rom_1 (.addr(controlled_buffer_33_out_2), .data(rom_1_data));  // open: sel
  assign {controlled_buffer_2_out_2, controlled_buffer_2_out} = decoder_9_out1 ? PC_q : 8'bz;  // Controlled_Buffer controlled_buffer_8
  Adder adder_1 (
    .a({pull_resistor_10_node_2, pull_resistor_10_node}), .b({pull_resistor_9_node_2, pull_resistor_9_node}),
    .out(adder_1_out));  // open: cin, cout
  assign controlled_buffer_9_out = decoder_6_out0 ? adder_1_out : 8'bz;  // Controlled_Buffer controlled_buffer_9
  assign controlled_buffer_6_out = decoder_3_out0 ? controlled_buffer_33_out : 4'bz;  // Controlled_Buffer controlled_buffer_10
  assign pull_resistor_2_node = and_2_out ? controlled_buffer_6_out[1:0] : 2'bz;  // Controlled_Buffer controlled_buffer_11
  assign pull_resistor_1_node = and_3_out ? controlled_buffer_6_out[1:0] : 2'bz;  // Controlled_Buffer controlled_buffer_12
  assign controlled_buffer_6_out = decoder_3_out1 ? pull_resistor_6_node : 4'bz;  // Controlled_Buffer controlled_buffer_13
  assign pull_resistor_2_node = decoder_8_out0 ? controlled_buffer_6_out[3:2] : 2'bz;  // Controlled_Buffer controlled_buffer_14
  not not_1 (not_1_out, controlled_buffer_28_out[15]);
  Counter counter_1 (
    .load(controlled_buffer_28_out[15]), .D(rom_1_data), .count(not_1_out), .Q(counter_1_q),
    .clk(clock_1_out), .clr(or_5_out));  // open: carry
  Clock clock_1 (.out(clock_1_out));
  not not_2 (not_2_out, controlled_buffer_28_out[13]);
  Register D0 (
    .D(controlled_buffer_1_out), .en(decoder_5_out1), .Q(D0_q), .clk(controlled_buffer_28_out[12]),
    .clr(or_5_out));
  assign {pull_resistor_10_node_2, pull_resistor_10_node} = decoder_1_out1 ? D0_q : 8'bz;  // Controlled_Buffer controlled_buffer_15
  assign {pull_resistor_9_node_2, pull_resistor_9_node} = decoder_2_out1 ? D0_q : 8'bz;  // Controlled_Buffer controlled_buffer_16
  Subtractor subtractor_1 (
    .a({pull_resistor_10_node_2, pull_resistor_10_node}), .b({pull_resistor_9_node_2, pull_resistor_9_node}),
    .out(subtractor_1_out));  // open: bin, bout
  assign controlled_buffer_9_out = decoder_6_out1 ? subtractor_1_out : 8'bz;  // Controlled_Buffer controlled_buffer_17
  assign pull_resistor_11_node = and_4_out ? controlled_buffer_6_out[1:0] : 2'bz;  // Controlled_Buffer controlled_buffer_18
  assign pull_resistor_12_node = and_1_out ? controlled_buffer_6_out[1:0] : 2'bz;  // Controlled_Buffer controlled_buffer_19
  and and_1 (and_1_out, decoder_7_out3, ~decoder_8_out3);  // AND_Gate
  assign pull_resistor_12_node = decoder_8_out3 ? controlled_buffer_6_out[3:2] : 2'bz;  // Controlled_Buffer controlled_buffer_20
  assign pull_resistor_1_node = decoder_8_out1 ? controlled_buffer_6_out[3:2] : 2'bz;  // Controlled_Buffer controlled_buffer_21
  assign pull_resistor_11_node = decoder_8_out2 ? controlled_buffer_6_out[3:2] : 2'bz;  // Controlled_Buffer controlled_buffer_22
  RAM #(.bus("separate")) ram_1 (
    .addr({controlled_buffer_2_out_2, controlled_buffer_2_out}),
    .din({pull_resistor_10_node_2, pull_resistor_10_node}), .data(ram_1_data),
    .str(controlled_buffer_28_out[13]), .clk(controlled_buffer_28_out[14]), .ld(not_2_out), .clr(and_5_out));  // open: sel
  assign controlled_buffer_1_out = decoder_4_out1 ? ram_1_data : 8'bz;  // Controlled_Buffer controlled_buffer_23
  Register D1 (
    .D(controlled_buffer_1_out), .en(decoder_5_out2), .Q(D1_q), .clk(controlled_buffer_28_out[12]),
    .clr(or_5_out));
  Pull_Resistor pull_resistor_19 (.node(pull_resistor_19_node));
  assign controlled_buffer_9_out = decoder_6_out2 ? pull_resistor_19_node : 8'bz;  // Controlled_Buffer controlled_buffer_24
  and and_2 (and_2_out, decoder_7_out0, ~decoder_8_out0);  // AND_Gate
  and and_3 (and_3_out, decoder_7_out1, ~decoder_8_out1);  // AND_Gate
  and and_4 (and_4_out, decoder_7_out2, ~decoder_8_out2);  // AND_Gate
  ROM #(.dataWidth(16)) rom_2 (.addr(counter_1_q), .data(rom_2_data));  // open: sel
  Hex_Digit_Display hex_digit_display_10 (.value(ram_1_data[3:0]));  // open: dp
  Hex_Digit_Display hex_digit_display_11 (.value(ram_1_data[7:4]));  // open: dp
  Pull_Resistor pull_resistor_20 (.node(controlled_buffer_1_out));
  assign {pull_resistor_9_node_2, pull_resistor_9_node} = decoder_2_out2 ? D1_q : 8'bz;  // Controlled_Buffer controlled_buffer_25
  assign {pull_resistor_10_node_2, pull_resistor_10_node} = decoder_1_out2 ? D1_q : 8'bz;  // Controlled_Buffer controlled_buffer_26
  Pull_Resistor #(.pull(1)) pull_resistor_21 (.node(pull_resistor_21_node));
  assign controlled_buffer_9_out = decoder_6_out3 ? pull_resistor_21_node : 8'bz;  // Controlled_Buffer controlled_buffer_27
  Pull_Resistor pull_resistor_22 (.node(controlled_buffer_9_out));
  or or_1 (or_1_out, decoder_8_out3, decoder_7_out3);
  or or_2 (or_2_out, decoder_8_out1, decoder_7_out1);
  or or_3 (or_3_out, decoder_8_out2, decoder_7_out2);
  Button button_1 (.out(button_1_out));
  assign {controlled_buffer_28_out[15:12], controlled_buffer_28_out_2, controlled_buffer_28_out[9:8], controlled_buffer_28_out_3, controlled_buffer_28_out_4} = not_3_out ? rom_2_data : 16'bz;  // Controlled_Buffer controlled_buffer_28
  not not_3 (not_3_out, manual_2);
  assign {controlled_buffer_28_out[15:12], controlled_buffer_28_out_2, controlled_buffer_28_out[9:8], controlled_buffer_28_out_3, controlled_buffer_28_out_4} = manual_2 ? register_1_q : 16'bz;  // Controlled_Buffer controlled_buffer_29
  assign controlled_buffer_1_out = decoder_4_out0 ? user_input : 8'bz;  // Controlled_Buffer controlled_buffer_30
  Register R0 (
    .D(controlled_buffer_9_out), .en(not_4_out), .Q(R0_q), .clk(controlled_buffer_28_out[12]), .clr(or_5_out));
  assign {pull_resistor_10_node_2, pull_resistor_10_node} = decoder_1_out3 ? R0_q : 8'bz;  // Controlled_Buffer controlled_buffer_31
  not not_4 (not_4_out, decoder_5_out3);
  Hex_Digit_Display hex_digit_display_12 (.value(controlled_buffer_9_out[3:0]));  // open: dp
  Hex_Digit_Display hex_digit_display_13 (.value(controlled_buffer_9_out[7:4]));  // open: dp
  or or_4 (or_4_out, decoder_8_out0, decoder_7_out0);
  Decoder #(.select(2)) decoder_7 (
    .out0(decoder_7_out0), .out1(decoder_7_out1), .out2(decoder_7_out2), .out3(decoder_7_out3),
    .sel(controlled_buffer_28_out_3[3:2]));  // open: en
  Decoder #(.select(2)) decoder_8 (
    .out0(decoder_8_out0), .out1(decoder_8_out1), .out2(decoder_8_out2), .out3(decoder_8_out3),
    .sel(controlled_buffer_28_out[9:8]));  // open: en
  Register #(.width(16)) register_1 (
    .D({in_7, in_8, in_9, in_10}), .en(pull_resistor_23_node), .Q(register_1_q), .clk(button_1_out));  // open: clr
  Pull_Resistor #(.pull(1)) pull_resistor_23 (.node(pull_resistor_23_node));
  Hex_Digit_Display hex_digit_display_14 (.value(user_input[7:4]));  // open: dp
  assign {pull_resistor_9_node_2, pull_resistor_9_node} = decoder_2_out3 ? R0_q : 8'bz;  // Controlled_Buffer controlled_buffer_32
  DotMatrix #(.inputtype("row"), .matrixcols(8), .matrixrows(1)) dotmatrix_2 (.row0(register_2_q));
  Button button_2 (.out(button_2_out));
  Pull_Resistor #(.pull(1)) pull_resistor_24 (.node(pull_resistor_24_node));
  Hex_Digit_Display hex_digit_display_15 (.value(user_input[3:0]));  // open: dp
  Hex_Digit_Display hex_digit_display_16 (.value(controlled_buffer_1_out[3:0]));  // open: dp
  Hex_Digit_Display hex_digit_display_17 (.value(controlled_buffer_1_out[7:4]));  // open: dp
  Register OC (
    .D(controlled_buffer_1_out), .en(decoder_5_out3), .Q(OC_q), .clk(controlled_buffer_28_out[12]),
    .clr(or_5_out));
  Register register_2 (
    .D({instr, sw0}), .en(pull_resistor_24_node), .Q(register_2_q), .clk(button_2_out), .clr(or_5_out));
  not not_5 (not_5_out, manual);
  assign {controlled_buffer_33_out_2, controlled_buffer_33_out} = not_5_out ? OC_q : 8'bz;  // Controlled_Buffer controlled_buffer_33
  assign {controlled_buffer_33_out_2, controlled_buffer_33_out} = manual ? register_2_q : 8'bz;  // Controlled_Buffer controlled_buffer_34
  Hex_Digit_Display hex_digit_display_18 (.value(controlled_buffer_28_out[15:12]));  // open: dp
  Hex_Digit_Display hex_digit_display_19 (.value(in_7));  // open: dp
  Counter PC (
    .load(controlled_buffer_28_out_4[3]), .D(controlled_buffer_1_out), .count(not_6_out), .Q(PC_q),
    .clk(controlled_buffer_28_out_4[2]), .clr(or_5_out));  // open: carry
  not not_6 (not_6_out, controlled_buffer_28_out_4[3]);
  Hex_Digit_Display hex_digit_display_20 (.value(controlled_buffer_28_out_3));  // open: dp
  Hex_Digit_Display hex_digit_display_21 (.value({controlled_buffer_28_out_2, controlled_buffer_28_out[9:8]}));  // open: dp
  Hex_Digit_Display hex_digit_display_22 (.value(in_8));  // open: dp
  Hex_Digit_Display hex_digit_display_23 (.value(in_9));  // open: dp
  and and_5 (and_5_out, ~mempersist, or_5_out);  // AND_Gate
  Decoder decoder_9 (.out0(decoder_9_out0), .out1(decoder_9_out1), .sel(controlled_buffer_28_out_4[1]));  // open: en
  Hex_Digit_Display hex_digit_display_24 (.value(controlled_buffer_28_out_4));  // open: dp
  Hex_Digit_Display hex_digit_display_25 (.value(in_10));  // open: dp
  or or_5 (or_5_out, controlled_buffer_28_out_4[0], reset);

  // Notes on the sheet:
  //   address
  //   op0
  //   op1
  //   #12: rck
  //   #13: mwr
  //   #14: mck
  //   data in
  //   op0
  //   swsw1
  //   swsw2
  //   free
  //   ld.ins.
  //   dsrc
  //   op1
  //   rwr
  //   swsw3
  //   free
  //   instr
  //   #10-11: swsw
  //   ROM (microvector)
  //   RAM (load the program here)
  //   sw1
  //   sw0
  //   contents of rom_1 (hex, n*v repeats v):
  //   0 10 20 30 40 50
  //   #15: luc
  //   ROM (microroutines)
  //   loadr rwr dsrc: 02c0 12c0
  //   loadm dsrc [op0]: 2300 6300
  //   add op0 op1: 0040 1040
  //   movr rwr: 0004 02c2 12c2
  //   jmp: 0004 03ca 03ce 0002 06c2 16c2 8000
  //   opcode
  //   contents of rom_2 (hex, n*v repeats v):
  //   2 6c2 16c2 8000 12*0 2c0 12c0 4 2 6c2 16c2 8000 9*0 2300 6300 4 2 6c2 16c2 8000 9*0 40 1040 4 2 6c2
  //   16c2 8000 9*0 4 2c2 12c2 4 2 6c2 16c2 8000 8*0 4 3ca 3ce 2 6c2 16c2 8000
  //   data out
  //   00: op0
  //   10: rwr
  //   01: op1
  //   11: dsrc
  //   #4-5
  //   opsel
  //   #6-7
  //   sw0
  //   #8-9
  //   sw1
  //   #1: asrc
  //   0: A0
  //   1: PC
  //   load microcode: 8000
  //   opcode
  //   sw1
  //   #3: lpc
  //   increment PC: 0004
  //   load instruction: 0002 06c2 16c2
  //   #2: pck
  //   #1: asrc
  //   #0: clr
  //   dsrc
  //   00: user input
  //   01: memory
  //   10: address
  //   11: op0 value
  //   op0, op1
  //   01: D0 (data)
  //   10: D1 (data)
  //   11: R0 (result)
  //   rwr
  //   01: D0 (data)
  //   10: D1 (data)
  //   00: A0 (address)
  //   00: A0 (address)
  //   11: OC (opcode)
endmodule
