// Logisim project cpuD.circ as structural Verilog: 1 circuit, main circuit main
module main (
  input  [7:0] in_1,
  input  manual,
  input  [3:0] instr,
  input  [3:0] sw0,
  input  manual_2,
  input  [3:0] in_6,
  input  [3:0] in_7,
  input  [3:0] in_8,
  input  [3:0] in_9,
  input  manual_3
);

  wire adder_1_cout, and_1_out, and_2_out, bitselector_1_out, button_1_out, button_2_out, clock_1_out,
       controlled_buffer_1_out, controlled_buffer_7_out, controlled_buffer_20_out, counter_2_carry,
       counter_3_carry, counter_4_carry, decoder_1_out0, decoder_1_out1, decoder_1_out2, decoder_1_out3,
       decoder_2_out0, decoder_2_out1, decoder_2_out2, decoder_2_out3, decoder_3_out0, decoder_3_out1,
       decoder_3_out2, decoder_3_out3, decoder_3_out4, decoder_3_out5, decoder_3_out6, decoder_3_out7,
       decoder_3_out8, decoder_3_out9, decoder_3_out10, decoder_3_out11, decoder_3_out12, decoder_3_out13,
       decoder_3_out14, decoder_3_out15, not_1_out, not_2_out, not_3_out, not_4_out, not_5_out, not_6_out,
       not_7_out, not_8_out, or_1_out, or_2_out, or_3_out, or_4_out, or_5_out, or_6_out, or_7_out,
       pull_resistor_1_node, pull_resistor_2_node, pull_resistor_4_node, pull_resistor_5_node,
       pull_resistor_6_node, pull_resistor_7_node, pull_resistor_12_node, pull_resistor_14_node,
       pull_resistor_16_node, subtractor_1_bout;
  wire [1:0] controlled_buffer_3_out, controlled_buffer_4_out, controlled_buffer_15_out_2,
       demultiplexer_1_out0, demultiplexer_1_out1, demultiplexer_1_out2, demultiplexer_1_out3;
  wire [2:0] pull_resistor_9_node;
  wire [3:0] controlled_buffer_15_out_3, controlled_buffer_15_out_4, controlled_buffer_21_out,
       controlled_buffer_21_out_2, controlled_buffer_23_out, controlled_buffer_23_out_2, counter_4_q,
       counter_4_q_2, pull_resistor_3_node;
  wire [7:0] adder_1_out, and_3_out, controlled_buffer_5_out, controlled_buffer_6_out,
       controlled_buffer_11_out, controlled_buffer_17_out, controlled_buffer_24_out, counter_1_q,
       counter_2_q, counter_3_q, nand_1_out, negator_1_out, nor_1_out, not_9_out, or_8_out,
       pull_resistor_13_node, ram_1_data, register_2_q, register_3_q, register_4_q, shifter_1_out,
       shifter_2_out, shifter_3_out, shifter_4_out, shifter_5_out, subtractor_1_out, xnor_1_out, xor_1_out;
  wire [15:0] register_1_q, rom_1_data;
  wire [15:10] controlled_buffer_15_out;

  not not_1 (not_1_out, controlled_buffer_15_out[13]);
  Decoder #(.select(2), .disabled(0)) decoder_1 (
    .out0(decoder_1_out0), .out1(decoder_1_out1), .out2(decoder_1_out2), .out3(decoder_1_out3),
    .sel(controlled_buffer_3_out), .en(controlled_buffer_1_out));
  assign controlled_buffer_1_out = or_2_out ? pull_resistor_1_node : 1'bz;  // Controlled_Buffer controlled_buffer_1
  assign controlled_buffer_1_out = or_1_out ? pull_resistor_2_node : 1'bz;  // Controlled_Buffer controlled_buffer_2
  assign controlled_buffer_3_out = or_1_out ? controlled_buffer_21_out[1:0] : 2'bz;  // Controlled_Buffer controlled_buffer_3
  RAM ram_1 (
    .addr(controlled_buffer_11_out), .data(ram_1_data), .clk(controlled_buffer_15_out[14]), .ld(not_1_out));  // open: sel, clr
  Pull_Resistor pull_resistor_1 (.node(pull_resistor_1_node));
  Pull_Resistor #(.pull(1)) pull_resistor_2 (.node(pull_resistor_2_node));
  or or_1 (or_1_out, decoder_2_out3, decoder_2_out1);
  or or_2 (or_2_out, decoder_2_out2, decoder_2_out0);
  assign controlled_buffer_4_out = decoder_2_out3 ? controlled_buffer_21_out[3:2] : 2'bz;  // Controlled_Buffer controlled_buffer_4
  Pull_Resistor pull_resistor_3 (.node(pull_resistor_3_node));
  assign controlled_buffer_5_out = not_3_out ? ram_1_data : 8'bz;  // Controlled_Buffer controlled_buffer_5
  assign controlled_buffer_6_out = decoder_1_out0 ? controlled_buffer_5_out : 8'bz;  // Controlled_Buffer controlled_buffer_6
  Demultiplexer #(.select(2), .width(2), .disabled(0)) demultiplexer_1 (
    .out0(demultiplexer_1_out0), .out1(demultiplexer_1_out1), .out2(demultiplexer_1_out2),
    .out3(demultiplexer_1_out3), .in(controlled_buffer_15_out_2), .sel(controlled_buffer_4_out),
    .en(controlled_buffer_7_out));
  Pull_Resistor pull_resistor_4 (.node(pull_resistor_4_node));
  assign controlled_buffer_7_out = or_3_out ? pull_resistor_4_node : 1'bz;  // Controlled_Buffer controlled_buffer_7
  assign controlled_buffer_7_out = or_4_out ? pull_resistor_5_node : 1'bz;  // Controlled_Buffer controlled_buffer_8
  Pull_Resistor #(.pull(1)) pull_resistor_5 (.node(pull_resistor_5_node));
  assign controlled_buffer_4_out = decoder_2_out2 ? controlled_buffer_21_out[1:0] : 2'bz;  // Controlled_Buffer controlled_buffer_9
  not not_2 (not_2_out, controlled_buffer_15_out[15]);
  Counter counter_1 (
    .load(controlled_buffer_15_out[15]), .D({controlled_buffer_21_out_2, pull_resistor_3_node}),
    .count(not_2_out), .Q(counter_1_q), .clk(clock_1_out), .clr(controlled_buffer_15_out[11]));  // open: carry
  Clock clock_1 (.out(clock_1_out));
  assign controlled_buffer_5_out = manual ? in_1 : 8'bz;  // Controlled_Buffer controlled_buffer_10
  not not_3 (not_3_out, manual);
  assign controlled_buffer_11_out = controlled_buffer_15_out[12] ? counter_2_q : 8'bz;  // Controlled_Buffer controlled_buffer_11
  Counter counter_2 (
    .load(demultiplexer_1_out0[1]), .D(controlled_buffer_6_out), .count(demultiplexer_1_out0[0]),
    .Q(counter_2_q), .carry(counter_2_carry), .clk(or_6_out), .clr(controlled_buffer_15_out[11]));
  Hex_Digit_Display hex_digit_display_1 (.value(in_1[3:0]));  // open: dp
  Hex_Digit_Display hex_digit_display_2 (.value(in_1[7:4]));  // open: dp
  assign controlled_buffer_6_out = decoder_1_out1 ? counter_2_q : 8'bz;  // Controlled_Buffer controlled_buffer_12
  or or_3 (or_3_out, decoder_2_out1, decoder_2_out0);
  or or_4 (or_4_out, decoder_2_out3, decoder_2_out2);
  ROM #(.dataWidth(16)) rom_1 (.addr(counter_1_q), .data(rom_1_data));  // open: sel
  assign controlled_buffer_6_out = decoder_1_out2 ? counter_3_q : 8'bz;  // Controlled_Buffer controlled_buffer_13
  assign controlled_buffer_11_out = not_4_out ? counter_3_q : 8'bz;  // Controlled_Buffer controlled_buffer_14
  not not_4 (not_4_out, controlled_buffer_15_out[12]);
  Counter counter_3 (
    .load(demultiplexer_1_out1[1]), .D(controlled_buffer_6_out), .count(demultiplexer_1_out1[0]),
    .Q(counter_3_q), .carry(counter_3_carry), .clk(or_6_out), .clr(controlled_buffer_15_out[11]));
  Decoder #(.select(2), .disabled(0), .enable("false")) decoder_2 (
    .out0(decoder_2_out0), .out1(decoder_2_out1), .out2(decoder_2_out2), .out3(decoder_2_out3),
    .sel(controlled_buffer_15_out_3[3:2]));
  Button button_1 (.out(button_1_out));
  assign {controlled_buffer_15_out, controlled_buffer_15_out_2, controlled_buffer_15_out_3, controlled_buffer_15_out_4} = not_5_out ? rom_1_data : 16'bz;  // Controlled_Buffer controlled_buffer_15
  not not_5 (not_5_out, manual_3);
  assign {controlled_buffer_15_out, controlled_buffer_15_out_2, controlled_buffer_15_out_3, controlled_buffer_15_out_4} = manual_3 ? register_1_q : 16'bz;  // Controlled_Buffer controlled_buffer_16
  assign controlled_buffer_17_out = not_6_out ? controlled_buffer_6_out : 8'bz;  // Controlled_Buffer controlled_buffer_17
  not not_6 (not_6_out, controlled_buffer_15_out_4[3]);
  or or_5 (or_5_out, counter_3_carry, counter_2_carry);
  assign controlled_buffer_17_out = controlled_buffer_15_out_4[3] ? {controlled_buffer_23_out_2, controlled_buffer_23_out} : 8'bz;  // Controlled_Buffer controlled_buffer_18
  or or_6 (or_6_out, and_1_out, controlled_buffer_15_out_3[1]);
  Register #(.width(16)) register_1 (
    .D({in_6, in_7, in_8, in_9}), .en(pull_resistor_6_node), .Q(register_1_q), .clk(button_1_out));  // open: clr
  Pull_Resistor #(.pull(1)) pull_resistor_6 (.node(pull_resistor_6_node));
  assign controlled_buffer_6_out = decoder_1_out3 ? {counter_4_q_2, counter_4_q} : 8'bz;  // Controlled_Buffer controlled_buffer_19
  Counter counter_4 (
    .load(demultiplexer_1_out2[1]), .D(controlled_buffer_17_out), .count(demultiplexer_1_out2[0]),
    .Q({counter_4_q_2, counter_4_q}), .carry(counter_4_carry), .clk(or_6_out),
    .clr(controlled_buffer_15_out[11]));
  or or_7 (or_7_out, counter_4_carry, or_5_out);
  assign controlled_buffer_20_out = controlled_buffer_21_out[3] ? bitselector_1_out : 1'bz;  // Controlled_Buffer controlled_buffer_20
  assign controlled_buffer_20_out = not_7_out ? ~bitselector_1_out : 1'bz;  // Controlled_Inverter controlled_inverter_1
  and and_1 (and_1_out, controlled_buffer_20_out, controlled_buffer_15_out_3[0]);
  not not_7 (not_7_out, controlled_buffer_21_out[3]);
  DotMatrix #(.inputtype("row"), .matrixcols(8), .matrixrows(1)) dotmatrix_1 (.row0(register_3_q));
  Button button_2 (.out(button_2_out));
  Pull_Resistor #(.pull(1)) pull_resistor_7 (.node(pull_resistor_7_node));
  BitSelector bitselector_1 (.in(register_4_q), .out(bitselector_1_out), .sel(controlled_buffer_21_out[2:0]));
  Hex_Digit_Display hex_digit_display_3 (.value(controlled_buffer_15_out[15:12]));  // open: dp
  Hex_Digit_Display hex_digit_display_4 (.value(in_6));  // open: dp
  Register register_2 (
    .D(controlled_buffer_6_out), .en(demultiplexer_1_out3[1]), .Q(register_2_q),
    .clk(controlled_buffer_15_out[10]), .clr(controlled_buffer_15_out[11]));
  not not_8 (not_8_out, manual_2);
  Register register_3 (.D({instr, sw0}), .en(pull_resistor_7_node), .Q(register_3_q), .clk(button_2_out));  // open: clr
  assign {controlled_buffer_21_out_2, controlled_buffer_21_out} = not_8_out ? register_2_q : 8'bz;  // Controlled_Buffer controlled_buffer_21
  assign {controlled_buffer_21_out_2, controlled_buffer_21_out} = manual_2 ? register_3_q : 8'bz;  // Controlled_Buffer controlled_buffer_22
  Hex_Digit_Display hex_digit_display_5 (.value(controlled_buffer_15_out_3));  // open: dp
  Hex_Digit_Display hex_digit_display_6 (.value({controlled_buffer_15_out[11:10], controlled_buffer_15_out_2}));  // open: dp
  Hex_Digit_Display hex_digit_display_7 (.value(in_8));  // open: dp
  Hex_Digit_Display hex_digit_display_8 (.value(in_7));  // open: dp
  Pull_Resistor pull_resistor_8 (.node(controlled_buffer_6_out));
  Register register_4 (
    .D(controlled_buffer_24_out), .en(demultiplexer_1_out3[0]), .Q(register_4_q),
    .clk(controlled_buffer_15_out[10]), .clr(controlled_buffer_15_out[11]));
  Hex_Digit_Display hex_digit_display_9 (.value(controlled_buffer_15_out_4));  // open: dp
  Hex_Digit_Display hex_digit_display_10 (.value(in_9));  // open: dp
  and and_2 (and_2_out, controlled_buffer_6_out[0], controlled_buffer_6_out[1], controlled_buffer_6_out[2], controlled_buffer_6_out[3], controlled_buffer_6_out[4], controlled_buffer_6_out[5], controlled_buffer_6_out[6], controlled_buffer_6_out[7]);
  Pull_Resistor #(.pull(1)) pull_resistor_9 (.node(pull_resistor_9_node[0]));
  Pull_Resistor pull_resistor_10 (.node(pull_resistor_9_node[1]));
  Pull_Resistor pull_resistor_11 (.node(pull_resistor_9_node[2]));
  Hex_Digit_Display hex_digit_display_11 (.value(controlled_buffer_23_out));  // open: dp
  Hex_Digit_Display hex_digit_display_12 (.value(controlled_buffer_23_out_2));  // open: dp
  Shifter shifter_1 (.in(controlled_buffer_6_out), .\dist (pull_resistor_9_node), .out(shifter_1_out));
  Shifter #(.shift("lr")) shifter_2 (.in(controlled_buffer_6_out), .\dist (pull_resistor_9_node), .out(shifter_2_out));
  Shifter #(.shift("ar")) shifter_3 (.in(controlled_buffer_6_out), .\dist (pull_resistor_9_node), .out(shifter_3_out));
  Shifter #(.shift("rl")) shifter_4 (.in(controlled_buffer_6_out), .\dist (pull_resistor_9_node), .out(shifter_4_out));
  Shifter #(.shift("rr")) shifter_5 (.in(controlled_buffer_6_out), .\dist (pull_resistor_9_node), .out(shifter_5_out));
  Negator negator_1 (.in(controlled_buffer_6_out), .out(negator_1_out));
  assign not_9_out = ~controlled_buffer_6_out;  // NOT_Gate not_9, 8 bits wide
  assign {controlled_buffer_23_out_2, controlled_buffer_23_out} = decoder_3_out0 ? shifter_1_out : 8'bz;  // Controlled_Buffer controlled_buffer_23
  assign controlled_buffer_24_out[0] = decoder_3_out0 ? controlled_buffer_6_out[7] : 1'bz;  // Controlled_Buffer controlled_buffer_24
  assign {controlled_buffer_23_out_2, controlled_buffer_23_out} = decoder_3_out1 ? shifter_2_out : 8'bz;  // Controlled_Buffer controlled_buffer_25
  assign controlled_buffer_24_out[0] = decoder_3_out1 ? controlled_buffer_6_out[0] : 1'bz;  // Controlled_Buffer controlled_buffer_26
  assign {controlled_buffer_23_out_2, controlled_buffer_23_out} = decoder_3_out2 ? shifter_3_out : 8'bz;  // Controlled_Buffer controlled_buffer_27
  assign controlled_buffer_24_out[0] = decoder_3_out2 ? controlled_buffer_6_out[0] : 1'bz;  // Controlled_Buffer controlled_buffer_28
  assign {controlled_buffer_23_out_2, controlled_buffer_23_out} = decoder_3_out3 ? shifter_4_out : 8'bz;  // Controlled_Buffer controlled_buffer_29
  assign controlled_buffer_24_out[0] = decoder_3_out3 ? controlled_buffer_6_out[7] : 1'bz;  // Controlled_Buffer controlled_buffer_30
  assign {controlled_buffer_23_out_2, controlled_buffer_23_out} = decoder_3_out4 ? shifter_5_out : 8'bz;  // Controlled_Buffer controlled_buffer_31
  assign controlled_buffer_24_out[0] = decoder_3_out4 ? controlled_buffer_6_out[0] : 1'bz;  // Controlled_Buffer controlled_buffer_32
  assign {controlled_buffer_23_out_2, controlled_buffer_23_out} = decoder_3_out5 ? negator_1_out : 8'bz;  // Controlled_Buffer controlled_buffer_33
  assign controlled_buffer_24_out[0] = decoder_3_out5 ? and_2_out : 1'bz;  // Controlled_Buffer controlled_buffer_34
  assign {controlled_buffer_23_out_2, controlled_buffer_23_out} = decoder_3_out6 ? not_9_out : 8'bz;  // Controlled_Buffer controlled_buffer_35
  assign controlled_buffer_24_out[0] = decoder_3_out6 ? pull_resistor_12_node : 1'bz;  // Controlled_Buffer controlled_buffer_36
  Pull_Resistor pull_resistor_12 (.node(pull_resistor_12_node));
  assign {controlled_buffer_23_out_2, controlled_buffer_23_out} = decoder_3_out7 ? pull_resistor_13_node : 8'bz;  // Controlled_Buffer controlled_buffer_37
  Pull_Resistor pull_resistor_13 (.node(pull_resistor_13_node));
  assign controlled_buffer_24_out[0] = decoder_3_out7 ? pull_resistor_14_node : 1'bz;  // Controlled_Buffer controlled_buffer_38
  Pull_Resistor pull_resistor_14 (.node(pull_resistor_14_node));
  Pull_Resistor pull_resistor_15 (.node(controlled_buffer_24_out[7:5]));
  Hex_Digit_Display hex_digit_display_13 (.value(controlled_buffer_6_out[7:4]));  // open: dp
  Decoder #(.select(4), .disabled(0), .enable("false")) decoder_3 (
    .out0(decoder_3_out0), .out1(decoder_3_out1), .out2(decoder_3_out2), .out3(decoder_3_out3),
    .out4(decoder_3_out4), .out5(decoder_3_out5), .out6(decoder_3_out6), .out7(decoder_3_out7),
    .out8(decoder_3_out8), .out9(decoder_3_out9), .out10(decoder_3_out10), .out11(decoder_3_out11),
    .out12(decoder_3_out12), .out13(decoder_3_out13), .out14(decoder_3_out14), .out15(decoder_3_out15),
    .sel({controlled_buffer_21_out_2[1:0], controlled_buffer_21_out[3:2]}));
  Hex_Digit_Display hex_digit_display_14 (.value(controlled_buffer_6_out[3:0]));  // open: dp
  Hex_Digit_Display hex_digit_display_15 (.value(counter_4_q_2));  // open: dp
  Hex_Digit_Display hex_digit_display_16 (.value(counter_4_q));  // open: dp
  Pull_Resistor pull_resistor_16 (.node(pull_resistor_16_node));
  Adder adder_1 (
    .a({counter_4_q_2, counter_4_q}), .b(controlled_buffer_6_out), .out(adder_1_out), .cout(adder_1_cout));  // open: cin
  Subtractor subtractor_1 (
    .a({counter_4_q_2, counter_4_q}), .b(controlled_buffer_6_out), .out(subtractor_1_out),
    .bout(subtractor_1_bout));  // open: bin
  assign and_3_out = {counter_4_q_2, counter_4_q} & controlled_buffer_6_out;  // AND_Gate and_3, 8 bits wide
  assign or_8_out = {counter_4_q_2, counter_4_q} | controlled_buffer_6_out;  // OR_Gate or_8, 8 bits wide
  assign xor_1_out = {counter_4_q_2, counter_4_q} ^ controlled_buffer_6_out;  // XOR_Gate xor_1, 8 bits wide
  assign nand_1_out = ~({counter_4_q_2, counter_4_q} & controlled_buffer_6_out);  // NAND_Gate nand_1, 8 bits wide
  assign nor_1_out = ~({counter_4_q_2, counter_4_q} | controlled_buffer_6_out);  // NOR_Gate nor_1, 8 bits wide
  assign xnor_1_out = ~({counter_4_q_2, counter_4_q} ^ controlled_buffer_6_out);  // XNOR_Gate xnor_1, 8 bits wide
  assign {controlled_buffer_23_out_2, controlled_buffer_23_out} = decoder_3_out8 ? adder_1_out : 8'bz;  // Controlled_Buffer controlled_buffer_39
  assign controlled_buffer_24_out[0] = decoder_3_out8 ? adder_1_cout : 1'bz;  // Controlled_Buffer controlled_buffer_40
  assign {controlled_buffer_23_out_2, controlled_buffer_23_out} = decoder_3_out9 ? subtractor_1_out : 8'bz;  // Controlled_Buffer controlled_buffer_41
  assign controlled_buffer_24_out[0] = decoder_3_out9 ? subtractor_1_bout : 1'bz;  // Controlled_Buffer controlled_buffer_42
  assign {controlled_buffer_23_out_2, controlled_buffer_23_out} = decoder_3_out10 ? and_3_out : 8'bz;  // Controlled_Buffer controlled_buffer_43
  assign controlled_buffer_24_out[0] = decoder_3_out10 ? pull_resistor_16_node : 1'bz;  // Controlled_Buffer controlled_buffer_44
  assign {controlled_buffer_23_out_2, controlled_buffer_23_out} = decoder_3_out11 ? or_8_out : 8'bz;  // Controlled_Buffer controlled_buffer_45
  assign controlled_buffer_24_out[0] = decoder_3_out11 ? pull_resistor_16_node : 1'bz;  // Controlled_Buffer controlled_buffer_46
  assign {controlled_buffer_23_out_2, controlled_buffer_23_out} = decoder_3_out12 ? xor_1_out : 8'bz;  // Controlled_Buffer controlled_buffer_47
  assign controlled_buffer_24_out[0] = decoder_3_out12 ? pull_resistor_16_node : 1'bz;  // Controlled_Buffer controlled_buffer_48
  assign {controlled_buffer_23_out_2, controlled_buffer_23_out} = decoder_3_out13 ? nand_1_out : 8'bz;  // Controlled_Buffer controlled_buffer_49
  assign controlled_buffer_24_out[0] = decoder_3_out13 ? pull_resistor_16_node : 1'bz;  // Controlled_Buffer controlled_buffer_50
  assign {controlled_buffer_23_out_2, controlled_buffer_23_out} = decoder_3_out14 ? nor_1_out : 8'bz;  // Controlled_Buffer controlled_buffer_51
  assign controlled_buffer_24_out[0] = decoder_3_out14 ? pull_resistor_16_node : 1'bz;  // Controlled_Buffer controlled_buffer_52
  assign {controlled_buffer_23_out_2, controlled_buffer_23_out} = decoder_3_out15 ? xnor_1_out : 8'bz;  // Controlled_Buffer controlled_buffer_53
  assign controlled_buffer_24_out[0] = decoder_3_out15 ? pull_resistor_16_node : 1'bz;  // Controlled_Buffer controlled_buffer_54
  and and_4 (controlled_buffer_24_out[1], ~controlled_buffer_23_out_2[3], ~controlled_buffer_23_out_2[2], ~controlled_buffer_23_out_2[1], ~controlled_buffer_23_out_2[0], ~controlled_buffer_23_out[3], ~controlled_buffer_23_out[2], ~controlled_buffer_23_out[1], ~controlled_buffer_23_out[0]);  // AND_Gate
  Comparator comparator_1 (
    .a(controlled_buffer_6_out), .b({counter_4_q_2, counter_4_q}), .gt(controlled_buffer_24_out[4]),
    .eq(controlled_buffer_24_out[3]), .lt(controlled_buffer_24_out[2]));

  // Notes on the sheet:
  //   address bus
  //   register ck
  //   clear
  //   address source: A0, PC
  //   memwr
  //   memck
  //   address source
  //   clear
  //   counter ck
  //   register ck
  //   dsrc: RAM, PC, A0, D0
  //   counter ck
  //   rcom: const, inc, set, dec
  //   OC+FL: on/off
  //   data source
  //   rcom: const, inc, set, dec
  //   OC+FL: on/off
  //   #10
  //   #11
  //   #12
  //   #14
  //   #8-9
  //   #13
  //   data bus
  //   rsel: PC, A0, D0, OC+FL
  //   #15: luc
  //   ROM (microroutines)
  //   PC
  //   OC
  //   contents of rom_1 (hex, n*v repeats v):
  //   2 6c2 16c2 8000 12*0 2c0 12c0 4 2 6c2 16c2 8000 9*0 2300 6300 4 2 6c2 16c2 8000 9*0 40 1040 4 2 6c2
  //   16c2 8000 9*0 4 2c2 12c2 4 2 6c2 16c2 8000 8*0 4 3ca 3ce 2 6c2 16c2 8000
  //   instr (OC 4-7)
  //   A0
  //   count/reg switch
  //   00: none
  //   01: data source
  //   10: rcom on LSN
  //   11: both
  //   #6-7
  //   D0
  //   selected flag
  //   (inverted to serve as ck)
  //   D0 src sel: data, result
  //   OC
  //   flagnum
  //   invert
  //   opcode
  //   sw1
  //   FL
  //   FL
  //   D0 src sel: data, result
  //   result
  //   ALU opsel
  //   0: SL
  //   1: SR
  //   2: SRA
  //   3: RL
  //   4: RR
  //   5: NEG
  //   6: NOT
  //   7: void
  //   8: ADD
  //   9: SUB
  //   a: AND
  //   b: OR
  //   c: XOR
  //   d: NAND
  //   e: NOR
  //   f: XNOR
  //   0: SL
  //   1: SR
  //   2: SRA
  //   3: RL
  //   4: RR
  //   5: NEG
  //   6: NOT
  //   carry
  //   zero
  //   lt
  //   eq
  //   gt
  //   data bus
  //   D0
  //   0: ADD
  //   1: SUB
  //   2: AND
  //   3: OR
  //   4: XOR
  //   5: NAND
  //   6: NOR
  //   7: XNOR
endmodule
