// Logisim project ftw.circ as structural Verilog: 1 circuit, main circuit main
module main (
  input  din3,
  input  din2,
  input  din1,
  input  din0,
  input  adr3,
  input  adr2,
  input  adr1,
  input  adr0,
  input  wr,
  input  rd,
  output dout3,
  output dout2,
  output dout1,
  output dout0
);

  wire and_1_out, and_2_out, and_3_out, and_4_out, and_5_out, and_6_out, and_7_out, and_8_out, and_9_out,
       and_10_out, and_11_out, and_12_out, main_1_dout0, main_1_dout1, main_2_dout0, main_2_dout1,
       main_3_dout0, main_3_dout1, main_5_dout0, main_5_dout1, main_6_dout0, main_6_dout1, main_7_dout0,
       main_7_dout1, undriven, undriven_2, undriven_3, undriven_4, undriven_5, undriven_6, undriven_7,
       undriven_8, undriven_9, undriven_10;

  and and_1 (and_1_out, undriven, ~undriven_2);  // AND_Gate
  and and_2 (and_2_out, adr3, ~adr2);  // AND_Gate
  and and_3 (and_3_out, ~adr3, adr2);  // AND_Gate
  mem2_main main_1 (
    .din1(undriven_5), .din0(undriven_6), .adr1(undriven_10), .adr0(undriven_9), .wr(and_4_out),
    .rd(and_9_out), .dout1(main_1_dout1), .dout0(main_1_dout0));
  and and_4 (and_4_out, and_1_out, undriven_3);
  mem2_main main_2 (
    .din1(din3), .din0(din2), .adr1(adr1), .adr0(adr0), .wr(and_5_out), .rd(and_10_out),
    .dout1(main_2_dout1), .dout0(main_2_dout0));
  and and_5 (and_5_out, and_2_out, wr);
  mem2_main main_3 (
    .din1(din3), .din0(din2), .adr1(adr1), .adr0(adr0), .wr(and_6_out), .rd(and_11_out),
    .dout1(main_3_dout1), .dout0(main_3_dout0));
  and and_6 (and_6_out, and_3_out, wr);
  mem2_main main_4 (
    .din1(din3), .din0(din2), .adr1(adr1), .adr0(adr0), .wr(and_7_out), .rd(and_12_out), .dout1(dout3),
    .dout0(dout2));
  and and_7 (and_7_out, and_8_out, wr);
  and and_8 (and_8_out, ~adr3, ~adr2);  // AND_Gate
  mem2_main main_5 (
    .din1(undriven_7), .din0(undriven_8), .adr1(undriven_10), .adr0(undriven_9), .wr(and_4_out),
    .rd(and_9_out), .dout1(main_5_dout1), .dout0(main_5_dout0));
  and and_9 (and_9_out, and_1_out, undriven_4);
  mem2_main main_6 (
    .din1(din1), .din0(din0), .adr1(adr1), .adr0(adr0), .wr(and_5_out), .rd(and_10_out),
    .dout1(main_6_dout1), .dout0(main_6_dout0));
  and and_10 (and_10_out, and_2_out, rd);
  mem2_main main_7 (
    .din1(din1), .din0(din0), .adr1(adr1), .adr0(adr0), .wr(and_6_out), .rd(and_11_out),
    .dout1(main_7_dout1), .dout0(main_7_dout0));
  and and_11 (and_11_out, and_3_out, rd);
  mem2_main main_8 (
    .din1(din1), .din0(din0), .adr1(adr1), .adr0(adr0), .wr(and_7_out), .rd(and_12_out), .dout1(dout1),
    .dout0(dout0));
  and and_12 (and_12_out, and_8_out, rd);
endmodule
