// Logisim project latch4.circ as structural Verilog: 1 circuit, main circuit main
module main (
  input  i3,
  input  i2,
  input  i1,
  input  i0,
  input  set,
  output o3,
  output o2,
  output o1,
  output o0
);

  wire nand_1_out, nand_2_out, nand_3_out, nand_4_out, nand_5_out, nand_6_out, nand_7_out, nand_8_out,
       nand_10_out, nand_12_out, nand_14_out, nand_16_out;

  nand nand_1 (nand_1_out, i3, set);
  nand nand_2 (nand_2_out, nand_1_out, set);
  nand nand_3 (nand_3_out, i2, set);
  nand nand_4 (nand_4_out, nand_3_out, set);
  nand nand_5 (nand_5_out, i1, set);
  nand nand_6 (nand_6_out, nand_5_out, set);
  nand nand_7 (nand_7_out, i0, set);
  nand nand_8 (nand_8_out, nand_7_out, set);
  nand nand_9 (o3, nand_1_out, nand_10_out);
  nand nand_10 (nand_10_out, o3, nand_2_out);
  nand nand_11 (o2, nand_3_out, nand_12_out);
  nand nand_12 (nand_12_out, o2, nand_4_out);
  nand nand_13 (o1, nand_5_out, nand_14_out);
  nand nand_14 (nand_14_out, o1, nand_6_out);
  nand nand_15 (o0, nand_7_out, nand_16_out);
  nand nand_16 (nand_16_out, o0, nand_8_out);
endmodule
