// Logisim project mem4x2.circ as structural Verilog: 1 circuit, main circuit main
module main (
  input  din3,
  input  din2,
  input  din1,
  input  din0,
  input  adr3,
  input  adr2,
  input  adr1,
  input  adr0,
  input  wr,
  input  rd,
  output dout3,
  output dout2,
  output dout1,
  output dout0
);

  wire and_1_out, and_2_out, and_3_out, and_4_out, and_5_out, and_6_out, and_7_out, and_8_out, and_9_out,
       and_10_out, and_11_out, and_12_out, and_13_out, and_14_out, and_15_out, and_16_out, and_17_out,
       and_18_out, and_19_out, and_20_out, and_21_out, and_22_out, and_23_out, and_24_out, and_25_out,
       and_26_out, and_27_out, and_28_out, main_1_dout0, main_1_dout1, main_2_dout0, main_2_dout1,
       main_3_dout0, main_3_dout1, main_4_dout0, main_4_dout1, main_5_dout0, main_5_dout1, main_6_dout0,
       main_6_dout1, main_7_dout0, main_7_dout1, main_8_dout0, main_8_dout1, nand_1_out, nand_2_out,
       nand_3_out, nand_4_out, nand_5_out, nand_6_out, nand_7_out, nand_8_out, nand_10_out, nand_12_out,
       nand_14_out, nand_16_out, or_1_out, or_2_out, or_3_out, or_4_out;

  and and_1 (and_1_out, adr3, adr2);
  and and_2 (and_2_out, adr3, ~adr2);  // AND_Gate
  and and_3 (and_3_out, ~adr3, adr2);  // AND_Gate
  and and_4 (and_4_out, ~adr3, ~adr2);  // AND_Gate
  mem2_main main_1 (
    .din1(din3), .din0(din2), .adr1(adr1), .adr0(adr0), .wr(and_5_out), .rd(and_9_out), .dout1(main_1_dout1),
    .dout0(main_1_dout0));
  and and_5 (and_5_out, and_1_out, wr);
  mem2_main main_2 (
    .din1(din3), .din0(din2), .adr1(adr1), .adr0(adr0), .wr(and_6_out), .rd(and_10_out),
    .dout1(main_2_dout1), .dout0(main_2_dout0));
  and and_6 (and_6_out, and_2_out, wr);
  mem2_main main_3 (
    .din1(din3), .din0(din2), .adr1(adr1), .adr0(adr0), .wr(and_7_out), .rd(and_11_out),
    .dout1(main_3_dout1), .dout0(main_3_dout0));
  and and_7 (and_7_out, and_3_out, wr);
  mem2_main main_4 (
    .din1(din3), .din0(din2), .adr1(adr1), .adr0(adr0), .wr(and_8_out), .rd(and_12_out),
    .dout1(main_4_dout1), .dout0(main_4_dout0));
  and and_8 (and_8_out, and_4_out, wr);
  mem2_main main_5 (
    .din1(din1), .din0(din0), .adr1(adr1), .adr0(adr0), .wr(and_5_out), .rd(and_9_out), .dout1(main_5_dout1),
    .dout0(main_5_dout0));
  and and_9 (and_9_out, and_1_out, rd);
  mem2_main main_6 (
    .din1(din1), .din0(din0), .adr1(adr1), .adr0(adr0), .wr(and_6_out), .rd(and_10_out),
    .dout1(main_6_dout1), .dout0(main_6_dout0));
  and and_10 (and_10_out, and_2_out, rd);
  mem2_main main_7 (
    .din1(din1), .din0(din0), .adr1(adr1), .adr0(adr0), .wr(and_7_out), .rd(and_11_out),
    .dout1(main_7_dout1), .dout0(main_7_dout0));
  and and_11 (and_11_out, and_3_out, rd);
  mem2_main main_8 (
    .din1(din1), .din0(din0), .adr1(adr1), .adr0(adr0), .wr(and_8_out), .rd(and_12_out),
    .dout1(main_8_dout1), .dout0(main_8_dout0));
  and and_12 (and_12_out, and_4_out, rd);
  and and_13 (and_13_out, main_1_dout1, and_1_out);
  and and_14 (and_14_out, main_1_dout0, and_1_out);
  and and_15 (and_15_out, main_5_dout1, and_1_out);
  and and_16 (and_16_out, main_5_dout0, and_1_out);
  and and_17 (and_17_out, main_2_dout1, and_2_out);
  and and_18 (and_18_out, main_2_dout0, and_2_out);
  and and_19 (and_19_out, main_6_dout1, and_2_out);
  and and_20 (and_20_out, main_6_dout0, and_2_out);
  and and_21 (and_21_out, main_3_dout1, and_3_out);
  and and_22 (and_22_out, main_3_dout0, and_3_out);
  and and_23 (and_23_out, main_7_dout1, and_3_out);
  and and_24 (and_24_out, main_7_dout0, and_3_out);
  and and_25 (and_25_out, main_4_dout1, and_4_out);
  and and_26 (and_26_out, main_4_dout0, and_4_out);
  and and_27 (and_27_out, main_8_dout1, and_4_out);
  and and_28 (and_28_out, main_8_dout0, and_4_out);
  or or_1 (or_1_out, and_16_out, and_20_out, and_24_out, and_28_out);
  or or_2 (or_2_out, and_14_out, and_18_out, and_22_out, and_26_out);
  or or_3 (or_3_out, and_15_out, and_19_out, and_23_out, and_27_out);
  or or_4 (or_4_out, and_13_out, and_17_out, and_21_out, and_25_out);
  nand nand_1 (nand_1_out, or_4_out, rd);
  nand nand_2 (nand_2_out, nand_1_out, rd);
  nand nand_3 (nand_3_out, or_2_out, rd);
  nand nand_4 (nand_4_out, nand_3_out, rd);
  nand nand_5 (nand_5_out, or_3_out, rd);
  nand nand_6 (nand_6_out, nand_5_out, rd);
  nand nand_7 (nand_7_out, or_1_out, rd);
  nand nand_8 (nand_8_out, nand_7_out, rd);
  nand nand_9 (dout3, nand_1_out, nand_10_out);
  nand nand_10 (nand_10_out, dout3, nand_2_out);
  nand nand_11 (dout2, nand_3_out, nand_12_out);
  nand nand_12 (nand_12_out, dout2, nand_4_out);
  nand nand_13 (dout1, nand_5_out, nand_14_out);
  nand nand_14 (nand_14_out, dout1, nand_6_out);
  nand nand_15 (dout0, nand_7_out, nand_16_out);
  nand nand_16 (nand_16_out, dout0, nand_8_out);
endmodule
