// Logisim project add4.circ as structural Verilog: 1 circuit, main circuit main
module main (
  input  b3,
  input  b2,
  input  b1,
  input  b0,
  input  a3,
  input  a2,
  input  a1,
  input  a0,
  output carry,
  output s3,
  output s2,
  output s1,
  output s0
);

  wire and_1_out, and_2_out, and_3_out, and_4_out, and_5_out, and_6_out, and_7_out, or_2_out, or_3_out,
       xor_1_out, xor_3_out, xor_5_out;

  and and_1 (and_1_out, xor_1_out, or_2_out);
  and and_2 (and_2_out, b3, a3);
  or or_1 (carry, and_2_out, and_1_out);
  and and_3 (and_3_out, b2, a2);
  xor xor_1 (xor_1_out, b3, a3);
  xor xor_2 (s3, xor_1_out, or_2_out);
  xor xor_3 (xor_3_out, b2, a2);
  and and_4 (and_4_out, xor_3_out, or_3_out);
  xor xor_4 (s2, xor_3_out, or_3_out);
  or or_2 (or_2_out, and_3_out, and_4_out);
  and and_5 (and_5_out, xor_5_out, and_7_out);
  and and_6 (and_6_out, b1, a1);
  or or_3 (or_3_out, and_6_out, and_5_out);
  xor xor_5 (xor_5_out, b1, a1);
  and and_7 (and_7_out, b0, a0);
  xor xor_6 (s1, xor_5_out, and_7_out);
  xor xor_7 (s0, b0, a0);
endmodule
