// Logisim project calc4.circ as structural Verilog: 1 circuit, main circuit main
module main (
  input  i3,
  input  i2,
  input  i1,
  input  i0,
  input  ld,
  input  a3,
  input  a2,
  input  a1,
  input  a0,
  input  wr,
  input  rd,
  input  acc
);

  wire and_1_out, and_2_out, and_3_out, and_4_out, and_5_out, and_6_out, and_7_out, and_8_out, main_3_carry;
  wire [3:0] main_1_dout0, main_2_o0, main_3_s0, or_4_out;

  Hex_Digit_Display hex_digit_display_1 (.value({i3, i2, i1, i0}));  // open: dp
  and and_1 (and_1_out, i3, ld);
  and and_2 (and_2_out, ~ld, main_3_s0[3]);  // AND_Gate
  and and_3 (and_3_out, i2, ld);
  and and_4 (and_4_out, ~ld, main_3_s0[2]);  // AND_Gate
  and and_5 (and_5_out, i1, ld);
  and and_6 (and_6_out, ~ld, main_3_s0[1]);  // AND_Gate
  and and_7 (and_7_out, i0, ld);
  and and_8 (and_8_out, ~ld, main_3_s0[0]);  // AND_Gate
  Hex_Digit_Display hex_digit_display_2 (.value({a3, a2, a1, a0}));  // open: dp
  Hex_Digit_Display hex_digit_display_3 (.value(or_4_out));  // open: dp
  or or_1 (or_4_out[3], and_1_out, and_2_out);
  or or_2 (or_4_out[2], and_3_out, and_4_out);
  or or_3 (or_4_out[1], and_5_out, and_6_out);
  or or_4 (or_4_out[0], and_7_out, and_8_out);
  mem4x2_main main_1 (
    .din3(or_4_out[3]), .din2(or_4_out[2]), .din1(or_4_out[1]), .din0(or_4_out[0]), .adr3(a3), .adr2(a2),
    .adr1(a1), .adr0(a0), .wr(wr), .rd(rd), .dout3(main_1_dout0[3]), .dout2(main_1_dout0[2]),
    .dout1(main_1_dout0[1]), .dout0(main_1_dout0[0]));
  latch4_main main_2 (
    .i3(main_1_dout0[3]), .i2(main_1_dout0[2]), .i1(main_1_dout0[1]), .i0(main_1_dout0[0]), .set(acc),
    .o3(main_2_o0[3]), .o2(main_2_o0[2]), .o1(main_2_o0[1]), .o0(main_2_o0[0]));
  add4_main main_3 (
    .b3(main_2_o0[3]), .b2(main_2_o0[2]), .b1(main_2_o0[1]), .b0(main_2_o0[0]), .a3(main_1_dout0[3]),
    .a2(main_1_dout0[2]), .a1(main_1_dout0[1]), .a0(main_1_dout0[0]), .carry(main_3_carry),
    .s3(main_3_s0[3]), .s2(main_3_s0[2]), .s1(main_3_s0[1]), .s0(main_3_s0[0]));
  Hex_Digit_Display hex_digit_display_4 (.value(main_1_dout0));  // open: dp
  Hex_Digit_Display hex_digit_display_5 (.value(main_2_o0));  // open: dp
  Hex_Digit_Display hex_digit_display_6 (.value(main_3_s0));  // open: dp
  LED led_1 (.in(main_3_carry));

  // Notes on the sheet:
  //   mem
  //   acc
  //   add
  //   oflo
endmodule
