// Logisim project cpuB.circ as structural Verilog: 1 circuit, main circuit main
module main (
  input  [7:0] ui0,
  input  [7:0] ui1,
  input  mck,
  input  mwr,
  input  clr,
  input  rck,
  input  [1:0] op0,
  input  [1:0] op1,
  input  [1:0] adr,
  input  [1:0] rwr,
  input  [2:0] src
);

  wire decoder_1_out0, decoder_1_out1, decoder_1_out2, decoder_1_out3, decoder_2_out0, decoder_2_out1,
       decoder_2_out2, decoder_2_out3, decoder_3_out0, decoder_3_out1, decoder_3_out2, decoder_3_out3,
       decoder_4_out0, decoder_4_out1, decoder_4_out2, decoder_4_out3, decoder_5_out0, decoder_5_out1,
       decoder_5_out2, decoder_5_out3, decoder_5_out4, decoder_5_out5, not_1_out;
  wire [7:0] adder_1_out, controlled_buffer_1_out, controlled_buffer_3_out, controlled_buffer_4_out,
       controlled_buffer_5_out, R0_q, R1_q, R2_q, R3_q, ram_1_data, rom_1_data, subtractor_1_out;

  Decoder #(.select(2)) decoder_1 (
    .out0(decoder_1_out0), .out1(decoder_1_out1), .out2(decoder_1_out2), .out3(decoder_1_out3), .sel(op0));  // open: en
  assign controlled_buffer_1_out = decoder_5_out5 ? ui1 : 8'bz;  // Controlled_Buffer controlled_buffer_1
  Decoder #(.select(2)) decoder_2 (
    .out0(decoder_2_out0), .out1(decoder_2_out1), .out2(decoder_2_out2), .out3(decoder_2_out3), .sel(op1));  // open: en
  Decoder #(.select(2)) decoder_3 (
    .out0(decoder_3_out0), .out1(decoder_3_out1), .out2(decoder_3_out2), .out3(decoder_3_out3), .sel(adr));  // open: en
  Decoder #(.select(2)) decoder_4 (
    .out0(decoder_4_out0), .out1(decoder_4_out1), .out2(decoder_4_out2), .out3(decoder_4_out3), .sel(rwr));  // open: en
  assign controlled_buffer_1_out = decoder_5_out4 ? ui0 : 8'bz;  // Controlled_Buffer controlled_buffer_2
  Decoder #(.select(3)) decoder_5 (
    .out0(decoder_5_out0), .out1(decoder_5_out1), .out2(decoder_5_out2), .out3(decoder_5_out3),
    .out4(decoder_5_out4), .out5(decoder_5_out5), .sel(src));  // open: out6, out7, en
  assign controlled_buffer_3_out = decoder_3_out0 ? R0_q : 8'bz;  // Controlled_Buffer controlled_buffer_3
  Register R0 (.D(controlled_buffer_1_out), .en(decoder_4_out0), .Q(R0_q), .clk(rck), .clr(clr));
  assign controlled_buffer_4_out = decoder_1_out0 ? R0_q : 8'bz;  // Controlled_Buffer controlled_buffer_4
  assign controlled_buffer_5_out = decoder_2_out0 ? R0_q : 8'bz;  // Controlled_Buffer controlled_buffer_5
  RAM #(.bus("separate")) ram_1 (
    .addr(controlled_buffer_3_out), .din(controlled_buffer_4_out), .data(ram_1_data), .str(mwr), .clk(mck),
    .ld(not_1_out), .clr(clr));  // open: sel
  not not_1 (not_1_out, mwr);
  Adder adder_1 (.a(controlled_buffer_4_out), .b(controlled_buffer_5_out), .out(adder_1_out));  // open: cin, cout
  assign controlled_buffer_1_out = decoder_5_out0 ? adder_1_out : 8'bz;  // Controlled_Buffer controlled_buffer_6
  assign controlled_buffer_1_out = decoder_5_out3 ? ram_1_data : 8'bz;  // Controlled_Buffer controlled_buffer_7
  assign controlled_buffer_3_out = decoder_3_out1 ? R1_q : 8'bz;  // Controlled_Buffer controlled_buffer_8
  Register R1 (.D(controlled_buffer_1_out), .en(decoder_4_out1), .Q(R1_q), .clk(rck), .clr(clr));
  assign controlled_buffer_4_out = decoder_1_out1 ? R1_q : 8'bz;  // Controlled_Buffer controlled_buffer_9
  assign controlled_buffer_5_out = decoder_2_out1 ? R1_q : 8'bz;  // Controlled_Buffer controlled_buffer_10
  Subtractor subtractor_1 (
    .a(controlled_buffer_4_out), .b(controlled_buffer_5_out), .out(subtractor_1_out));  // open: bin, bout
  assign controlled_buffer_1_out = decoder_5_out1 ? subtractor_1_out : 8'bz;  // Controlled_Buffer controlled_buffer_11
  Register R2 (.D(controlled_buffer_1_out), .en(decoder_4_out2), .Q(R2_q), .clk(rck), .clr(clr));
  ROM rom_1 (.addr(controlled_buffer_3_out), .data(rom_1_data));  // open: sel
  assign controlled_buffer_1_out = decoder_5_out2 ? rom_1_data : 8'bz;  // Controlled_Buffer controlled_buffer_12
  assign controlled_buffer_3_out = decoder_3_out2 ? R2_q : 8'bz;  // Controlled_Buffer controlled_buffer_13
  assign controlled_buffer_5_out = decoder_2_out2 ? R2_q : 8'bz;  // Controlled_Buffer controlled_buffer_14
  assign controlled_buffer_4_out = decoder_1_out2 ? R2_q : 8'bz;  // Controlled_Buffer controlled_buffer_15
  Register R3 (.D(controlled_buffer_1_out), .en(decoder_4_out3), .Q(R3_q), .clk(rck), .clr(clr));
  assign controlled_buffer_3_out = decoder_3_out3 ? R3_q : 8'bz;  // Controlled_Buffer controlled_buffer_16
  assign controlled_buffer_5_out = decoder_2_out3 ? R3_q : 8'bz;  // Controlled_Buffer controlled_buffer_17
  assign controlled_buffer_4_out = decoder_1_out3 ? R3_q : 8'bz;  // Controlled_Buffer controlled_buffer_18
endmodule
