// Logisim project cpuC.circ as structural Verilog: 1 circuit, main circuit main
module main (
  input  [7:0] user_input,
  input  manual,
  input  [7:0] opsel,
  input  reset,
  input  [7:0] in_5,
  input  [7:0] in_6,
  input  manual_2
);

  wire and_1_out, and_2_out, and_3_out, and_4_out, clock_1_out, decoder_1_out0, decoder_1_out1,
       decoder_1_out2, decoder_1_out3, decoder_2_out0, decoder_2_out1, decoder_2_out2, decoder_2_out3,
       decoder_3_out0, decoder_3_out1, decoder_3_out2, decoder_3_out3, decoder_4_out0, decoder_4_out1,
       decoder_4_out2, decoder_4_out3, decoder_5_out0, decoder_5_out1, decoder_5_out2, decoder_5_out3,
       decoder_6_out0, decoder_6_out1, decoder_6_out2, decoder_6_out3, decoder_7_out0, decoder_7_out1,
       decoder_7_out2, decoder_7_out3, decoder_8_out0, decoder_8_out1, decoder_8_out2, decoder_8_out3,
       decoder_9_out0, decoder_9_out1, not_1_out, not_2_out, not_3_out, not_4_out, not_5_out, or_1_out,
       pull_resistor_19_node;
  wire [1:0] controlled_buffer_28_out_2, controlled_buffer_28_out_3, pull_resistor_1_node,
       pull_resistor_8_node, pull_resistor_9_node, pull_resistor_10_node;
  wire [3:0] controlled_buffer_2_out, controlled_buffer_2_out_2, controlled_buffer_5_out,
       controlled_buffer_5_out_2, controlled_buffer_6_out, controlled_buffer_28_out_4,
       controlled_buffer_33_out, controlled_buffer_33_out_2, pull_resistor_7_node, pull_resistor_13_node,
       pull_resistor_15_node;
  wire [7:0] A0_q, adder_1_out, controlled_buffer_1_out, controlled_buffer_4_out, controlled_buffer_8_out,
       counter_1_q, D0_q, D1_q, OC_q, PC_q, pull_resistor_17_node, pull_resistor_18_node, R0_q, ram_1_data,
       rom_1_data, subtractor_1_out;
  wire [15:0] rom_2_data;
  wire [15:6] controlled_buffer_28_out;

  Hex_Digit_Display hex_digit_display_1 (.value(controlled_buffer_2_out_2));  // open: dp
  Hex_Digit_Display hex_digit_display_2 (.value(controlled_buffer_2_out));  // open: dp
  Hex_Digit_Display hex_digit_display_3 (.value(controlled_buffer_5_out_2));  // open: dp
  Decoder #(.select(2)) decoder_1 (
    .out0(decoder_1_out0), .out1(decoder_1_out1), .out2(decoder_1_out2), .out3(decoder_1_out3),
    .sel(pull_resistor_1_node));  // open: en
  Pull_Resistor pull_resistor_1 (.node(pull_resistor_1_node));
  Decoder #(.select(2)) decoder_2 (
    .out0(decoder_2_out0), .out1(decoder_2_out1), .out2(decoder_2_out2), .out3(decoder_2_out3),
    .sel(controlled_buffer_28_out_2));  // open: en
  Pull_Resistor pull_resistor_2 (.node(pull_resistor_15_node[2]));
  Pull_Resistor #(.pull(1)) pull_resistor_3 (.node(pull_resistor_7_node[3]));
  Pull_Resistor #(.pull(1)) pull_resistor_4 (.node(pull_resistor_7_node[2]));
  Pull_Resistor pull_resistor_5 (.node(pull_resistor_7_node[1]));
  Pull_Resistor pull_resistor_6 (.node(pull_resistor_15_node[3]));
  Pull_Resistor #(.pull(1)) pull_resistor_7 (.node(pull_resistor_7_node[0]));
  Hex_Digit_Display hex_digit_display_4 (.value(controlled_buffer_5_out));  // open: dp
  Decoder #(.select(2)) decoder_3 (
    .out0(decoder_3_out0), .out1(decoder_3_out1), .out2(decoder_3_out2), .out3(decoder_3_out3),
    .sel(pull_resistor_10_node));  // open: en
  Decoder #(.select(2)) decoder_4 (
    .out0(decoder_4_out0), .out1(decoder_4_out1), .out2(decoder_4_out2), .out3(decoder_4_out3),
    .sel(pull_resistor_9_node));  // open: en
  Decoder #(.select(2)) decoder_5 (
    .out0(decoder_5_out0), .out1(decoder_5_out1), .out2(decoder_5_out2), .out3(decoder_5_out3),
    .sel(pull_resistor_8_node));  // open: en
  Pull_Resistor pull_resistor_8 (.node(pull_resistor_8_node));
  Pull_Resistor pull_resistor_9 (.node(pull_resistor_9_node));
  Pull_Resistor pull_resistor_10 (.node(pull_resistor_10_node));
  Pull_Resistor pull_resistor_11 (.node(pull_resistor_15_node[1]));
  Pull_Resistor pull_resistor_12 (.node(pull_resistor_13_node[2]));
  Pull_Resistor pull_resistor_13 (.node(pull_resistor_13_node[0]));
  Pull_Resistor pull_resistor_14 (.node(pull_resistor_13_node[3]));
  Pull_Resistor pull_resistor_15 (.node(pull_resistor_15_node[0]));
  Pull_Resistor pull_resistor_16 (.node(pull_resistor_13_node[1]));
  assign controlled_buffer_1_out = decoder_3_out3 ? {controlled_buffer_5_out_2, controlled_buffer_5_out} : 8'bz;  // Controlled_Buffer controlled_buffer_1
  assign {controlled_buffer_2_out_2, controlled_buffer_2_out} = decoder_9_out0 ? A0_q : 8'bz;  // Controlled_Buffer controlled_buffer_2
  assign controlled_buffer_1_out = decoder_3_out2 ? A0_q : 8'bz;  // Controlled_Buffer controlled_buffer_3
  Register A0 (
    .D(controlled_buffer_1_out), .en(decoder_5_out0), .Q(A0_q), .clk(controlled_buffer_28_out[12]),
    .clr(or_1_out));
  assign controlled_buffer_4_out = decoder_4_out0 ? A0_q : 8'bz;  // Controlled_Buffer controlled_buffer_4
  assign {controlled_buffer_5_out_2, controlled_buffer_5_out} = decoder_1_out0 ? A0_q : 8'bz;  // Controlled_Buffer controlled_buffer_5
  Decoder #(.select(2)) decoder_6 (
    .out0(decoder_6_out0), .out1(decoder_6_out1), .out2(decoder_6_out2), .out3(decoder_6_out3),
    .sel(controlled_buffer_28_out_3));  // open: en
  assign controlled_buffer_6_out = decoder_2_out3 ? pull_resistor_13_node : 4'bz;  // Controlled_Buffer controlled_buffer_6
  ROM #(.addrWidth(4)) rom_1 (.addr(controlled_buffer_33_out_2), .data(rom_1_data));  // open: sel
  assign {controlled_buffer_2_out_2, controlled_buffer_2_out} = decoder_9_out1 ? PC_q : 8'bz;  // Controlled_Buffer controlled_buffer_7
  Adder adder_1 (
    .a({controlled_buffer_5_out_2, controlled_buffer_5_out}), .b(controlled_buffer_4_out), .out(adder_1_out));  // open: cin, cout
  assign controlled_buffer_8_out = decoder_6_out0 ? adder_1_out : 8'bz;  // Controlled_Buffer controlled_buffer_8
  assign controlled_buffer_6_out = decoder_2_out0 ? controlled_buffer_33_out : 4'bz;  // Controlled_Buffer controlled_buffer_9
  assign pull_resistor_1_node = and_3_out ? controlled_buffer_6_out[1:0] : 2'bz;  // Controlled_Buffer controlled_buffer_10
  assign controlled_buffer_6_out = decoder_2_out1 ? pull_resistor_7_node : 4'bz;  // Controlled_Buffer controlled_buffer_11
  assign controlled_buffer_6_out = decoder_2_out2 ? pull_resistor_15_node : 4'bz;  // Controlled_Buffer controlled_buffer_12
  not not_1 (not_1_out, controlled_buffer_28_out[15]);
  Counter counter_1 (
    .load(controlled_buffer_28_out[15]), .D(rom_1_data), .count(not_1_out), .Q(counter_1_q),
    .clk(clock_1_out), .clr(or_1_out));  // open: carry
  Clock clock_1 (.out(clock_1_out));
  not not_2 (not_2_out, controlled_buffer_28_out[13]);
  Register D0 (
    .D(controlled_buffer_1_out), .en(decoder_5_out1), .Q(D0_q), .clk(controlled_buffer_28_out[12]),
    .clr(or_1_out));
  assign {controlled_buffer_5_out_2, controlled_buffer_5_out} = decoder_1_out1 ? D0_q : 8'bz;  // Controlled_Buffer controlled_buffer_13
  assign controlled_buffer_4_out = decoder_4_out1 ? D0_q : 8'bz;  // Controlled_Buffer controlled_buffer_14
  Subtractor subtractor_1 (
    .a({controlled_buffer_5_out_2, controlled_buffer_5_out}), .b(controlled_buffer_4_out),
    .out(subtractor_1_out));  // open: bin, bout
  assign controlled_buffer_8_out = decoder_6_out1 ? subtractor_1_out : 8'bz;  // Controlled_Buffer controlled_buffer_15
  assign pull_resistor_8_node = and_1_out ? controlled_buffer_6_out[1:0] : 2'bz;  // Controlled_Buffer controlled_buffer_16
  assign pull_resistor_9_node = and_4_out ? controlled_buffer_6_out[1:0] : 2'bz;  // Controlled_Buffer controlled_buffer_17
  assign pull_resistor_1_node = decoder_8_out0 ? controlled_buffer_6_out[3:2] : 2'bz;  // Controlled_Buffer controlled_buffer_18
  assign pull_resistor_9_node = decoder_8_out1 ? controlled_buffer_6_out[3:2] : 2'bz;  // Controlled_Buffer controlled_buffer_19
  RAM #(.bus("separate")) ram_1 (
    .addr({controlled_buffer_2_out_2, controlled_buffer_2_out}),
    .din({controlled_buffer_5_out_2, controlled_buffer_5_out}), .data(ram_1_data),
    .str(controlled_buffer_28_out[13]), .clk(controlled_buffer_28_out[14]), .ld(not_2_out), .clr(or_1_out));  // open: sel
  assign controlled_buffer_1_out = decoder_3_out1 ? ram_1_data : 8'bz;  // Controlled_Buffer controlled_buffer_20
  Register D1 (
    .D(controlled_buffer_1_out), .en(decoder_5_out2), .Q(D1_q), .clk(controlled_buffer_28_out[12]),
    .clr(or_1_out));
  Pull_Resistor pull_resistor_17 (.node(pull_resistor_17_node));
  assign controlled_buffer_8_out = decoder_6_out2 ? pull_resistor_17_node : 8'bz;  // Controlled_Buffer controlled_buffer_21
  and and_1 (and_1_out, decoder_7_out2, ~decoder_8_out2);  // AND_Gate
  assign pull_resistor_10_node = and_2_out ? controlled_buffer_6_out[1:0] : 2'bz;  // Controlled_Buffer controlled_buffer_22
  and and_2 (and_2_out, decoder_7_out3, ~decoder_8_out3);  // AND_Gate
  assign pull_resistor_8_node = decoder_8_out2 ? controlled_buffer_6_out[3:2] : 2'bz;  // Controlled_Buffer controlled_buffer_23
  assign pull_resistor_10_node = decoder_8_out3 ? controlled_buffer_6_out[3:2] : 2'bz;  // Controlled_Buffer controlled_buffer_24
  ROM #(.dataWidth(16)) rom_2 (.addr(counter_1_q), .data(rom_2_data));  // open: sel
  Hex_Digit_Display hex_digit_display_5 (.value(ram_1_data[3:0]));  // open: dp
  Hex_Digit_Display hex_digit_display_6 (.value(ram_1_data[7:4]));  // open: dp
  assign controlled_buffer_4_out = decoder_4_out2 ? D1_q : 8'bz;  // Controlled_Buffer controlled_buffer_25
  assign {controlled_buffer_5_out_2, controlled_buffer_5_out} = decoder_1_out2 ? D1_q : 8'bz;  // Controlled_Buffer controlled_buffer_26
  Pull_Resistor #(.pull(1)) pull_resistor_18 (.node(pull_resistor_18_node));
  assign controlled_buffer_8_out = decoder_6_out3 ? pull_resistor_18_node : 8'bz;  // Controlled_Buffer controlled_buffer_27
  and and_3 (and_3_out, decoder_7_out0, ~decoder_8_out0);  // AND_Gate
  and and_4 (and_4_out, decoder_7_out1, ~decoder_8_out1);  // AND_Gate
  assign {controlled_buffer_28_out[15:12], controlled_buffer_28_out_2, controlled_buffer_28_out[9:6], controlled_buffer_28_out_3, controlled_buffer_28_out_4} = manual_2 ? {in_5, in_6} : 16'bz;  // Controlled_Buffer controlled_buffer_28
  not not_3 (not_3_out, manual_2);
  assign {controlled_buffer_28_out[15:12], controlled_buffer_28_out_2, controlled_buffer_28_out[9:6], controlled_buffer_28_out_3, controlled_buffer_28_out_4} = not_3_out ? rom_2_data : 16'bz;  // Controlled_Buffer controlled_buffer_29
  assign controlled_buffer_1_out = decoder_3_out0 ? user_input : 8'bz;  // Controlled_Buffer controlled_buffer_30
  Register R0 (
    .D(controlled_buffer_8_out), .en(pull_resistor_19_node), .Q(R0_q), .clk(controlled_buffer_28_out[12]),
    .clr(or_1_out));
  Pull_Resistor #(.pull(1)) pull_resistor_19 (.node(pull_resistor_19_node));
  assign {controlled_buffer_5_out_2, controlled_buffer_5_out} = decoder_1_out3 ? R0_q : 8'bz;  // Controlled_Buffer controlled_buffer_31
  Hex_Digit_Display hex_digit_display_7 (.value(controlled_buffer_8_out[7:4]));  // open: dp
  Decoder #(.select(2)) decoder_7 (
    .out0(decoder_7_out0), .out1(decoder_7_out1), .out2(decoder_7_out2), .out3(decoder_7_out3),
    .sel(controlled_buffer_28_out[7:6]));  // open: en
  Decoder #(.select(2)) decoder_8 (
    .out0(decoder_8_out0), .out1(decoder_8_out1), .out2(decoder_8_out2), .out3(decoder_8_out3),
    .sel(controlled_buffer_28_out[9:8]));  // open: en
  Hex_Digit_Display hex_digit_display_8 (.value(user_input[7:4]));  // open: dp
  assign controlled_buffer_4_out = decoder_4_out3 ? R0_q : 8'bz;  // Controlled_Buffer controlled_buffer_32
  Hex_Digit_Display hex_digit_display_9 (.value(controlled_buffer_8_out[3:0]));  // open: dp
  assign {controlled_buffer_33_out_2, controlled_buffer_33_out} = not_4_out ? OC_q : 8'bz;  // Controlled_Buffer controlled_buffer_33
  not not_4 (not_4_out, manual);
  assign {controlled_buffer_33_out_2, controlled_buffer_33_out} = manual ? opsel : 8'bz;  // Controlled_Buffer controlled_buffer_34
  Hex_Digit_Display hex_digit_display_10 (.value(user_input[3:0]));  // open: dp
  Hex_Digit_Display hex_digit_display_11 (.value(controlled_buffer_1_out[3:0]));  // open: dp
  Hex_Digit_Display hex_digit_display_12 (.value(controlled_buffer_1_out[7:4]));  // open: dp
  Register OC (
    .D(controlled_buffer_1_out), .en(decoder_5_out3), .Q(OC_q), .clk(controlled_buffer_28_out[12]),
    .clr(or_1_out));
  Hex_Digit_Display hex_digit_display_13 (.value(controlled_buffer_28_out[15:12]));  // open: dp
  Hex_Digit_Display hex_digit_display_14 (.value({controlled_buffer_28_out_2, controlled_buffer_28_out[9:8]}));  // open: dp
  Counter PC (
    .load(controlled_buffer_28_out_4[3]), .D(controlled_buffer_1_out), .count(not_5_out), .Q(PC_q),
    .clk(controlled_buffer_28_out_4[2]), .clr(or_1_out));  // open: carry
  not not_5 (not_5_out, controlled_buffer_28_out_4[3]);
  Hex_Digit_Display hex_digit_display_15 (.value({controlled_buffer_28_out[7:6], controlled_buffer_28_out_3}));  // open: dp
  Hex_Digit_Display hex_digit_display_16 (.value(controlled_buffer_28_out_4));  // open: dp
  Decoder decoder_9 (.out0(decoder_9_out0), .out1(decoder_9_out1), .sel(controlled_buffer_28_out_4[1]));  // open: en
  or or_1 (or_1_out, controlled_buffer_28_out_4[0], reset);

  // Notes on the sheet:
  //   address
  //   #14: mck
  //   data in
  //   op0
  //   #12: rck
  //   #13: mwr
  //   swsw2
  //   swsw1
  //   ld.ins.
  //   free
  //   dsrc
  //   op1
  //   rwr
  //   swsw3
  //   free
  //   dsrc
  //   00: user input
  //   01: memory
  //   10: address
  //   11: op0 value
  //   op0, op1
  //   00: A0 (address)
  //   01: D0 (data)
  //   10: D1 (data)
  //   11: R0 (result)
  //   instr
  //   #10-11: swsw
  //   rwr
  //   00: A0 (address)
  //   01: D0 (data)
  //   10: D1 (data)
  //   11: OC (opcode)
  //   contents of rom_1 (hex, n*v repeats v):
  //   5*0 db
  //   #15: luc
  //   increment PC: 0004
  //   mv to reg (rwr dsrc): 02c0 12c0
  //   mv to mem (dsrc [op0]): 2300 6300
  //   load instruction: 0002 06c2 16c2
  //   data out
  //   00: op0
  //   10: rwr
  //   01: op1
  //   11: dsrc
  //   #4-5
  //   #6-7
  //   sw0
  //   #8-9
  //   sw1
  //   #1: asrc
  //   0: A0
  //   1: PC
  //   opcode
  //   #3: lpc
  //   #2: pck
  //   #1: asrc
  //   #0: clr
endmodule
