// Logisim project first-steps.circ as structural Verilog: 1 circuit, main circuit main
module main (
  input  in_1,
  input  in_2,
  input  in_3,
  input  in_4,
  input  in_5,
  input  in_6,
  output out_7,
  output out_8,
  output out_9,
  output out_10,
  output out_11
);

  wire and_1_out, and_2_out, and_3_out, and_4_out, and_5_out, and_6_out, not_1_out, not_2_out, not_5_out,
       not_6_out, or_1_out, or_2_out;

  or or_1 (or_1_out, in_3, out_9);
  or or_2 (or_2_out, out_8, in_4);
  not not_1 (not_1_out, in_1);
  not not_2 (not_2_out, in_2);
  not not_3 (out_8, or_1_out);
  not not_4 (out_9, or_2_out);
  and and_1 (and_1_out, in_5, in_6);
  and and_2 (and_2_out, not_5_out, in_6);
  and and_3 (and_3_out, not_1_out, in_2);
  and and_4 (and_4_out, in_1, not_2_out);
  not not_5 (not_5_out, and_1_out);
  not not_6 (not_6_out, and_2_out);
  or or_3 (out_7, and_3_out, and_4_out);
  not not_7 (out_10, and_5_out);
  and and_5 (and_5_out, not_5_out, out_11);
  not not_8 (out_11, and_6_out);
  and and_6 (and_6_out, out_10, not_6_out);

  // Notes on the sheet:
  //   XOR
  //   SR latch
  //   gated D latch
endmodule
