// Logisim project latch8.circ as structural Verilog: 1 circuit, main circuit main
module main (
  input  i7,
  input  i6,
  input  i5,
  input  i4,
  input  i3,
  input  i2,
  input  i1,
  input  i0,
  input  set,
  output o7,
  output o6,
  output o5,
  output o4,
  output o3,
  output o2,
  output o1,
  output o0
);

  wire nand_1_out, nand_2_out, nand_3_out, nand_4_out, nand_5_out, nand_6_out, nand_7_out, nand_8_out,
       nand_9_out, nand_10_out, nand_11_out, nand_12_out, nand_13_out, nand_14_out, nand_15_out, nand_16_out,
       nand_18_out, nand_20_out, nand_22_out, nand_24_out, nand_26_out, nand_28_out, nand_30_out, nand_32_out;

  nand nand_1 (nand_1_out, i7, set);
  nand nand_2 (nand_2_out, nand_1_out, set);
  nand nand_3 (nand_3_out, i6, set);
  nand nand_4 (nand_4_out, nand_3_out, set);
  nand nand_5 (nand_5_out, i5, set);
  nand nand_6 (nand_6_out, nand_5_out, set);
  nand nand_7 (nand_7_out, i4, set);
  nand nand_8 (nand_8_out, nand_7_out, set);
  nand nand_9 (nand_9_out, i3, set);
  nand nand_10 (nand_10_out, nand_9_out, set);
  nand nand_11 (nand_11_out, i2, set);
  nand nand_12 (nand_12_out, nand_11_out, set);
  nand nand_13 (nand_13_out, i1, set);
  nand nand_14 (nand_14_out, nand_13_out, set);
  nand nand_15 (nand_15_out, i0, set);
  nand nand_16 (nand_16_out, nand_15_out, set);
  nand nand_17 (o7, nand_1_out, nand_18_out);
  nand nand_18 (nand_18_out, o7, nand_2_out);
  nand nand_19 (o6, nand_3_out, nand_20_out);
  nand nand_20 (nand_20_out, o6, nand_4_out);
  nand nand_21 (o5, nand_5_out, nand_22_out);
  nand nand_22 (nand_22_out, o5, nand_6_out);
  nand nand_23 (o4, nand_7_out, nand_24_out);
  nand nand_24 (nand_24_out, o4, nand_8_out);
  nand nand_25 (o3, nand_9_out, nand_26_out);
  nand nand_26 (nand_26_out, o3, nand_10_out);
  nand nand_27 (o2, nand_11_out, nand_28_out);
  nand nand_28 (nand_28_out, o2, nand_12_out);
  nand nand_29 (o1, nand_13_out, nand_30_out);
  nand nand_30 (nand_30_out, o1, nand_14_out);
  nand nand_31 (o0, nand_15_out, nand_32_out);
  nand nand_32 (nand_32_out, o0, nand_16_out);
endmodule
