// Logisim project mem2.circ as structural Verilog: 1 circuit, main circuit main
module main (
  input  din1,
  input  din0,
  input  adr1,
  input  adr0,
  input  wr,
  input  rd,
  output dout1,
  output dout0
);

  wire and_1_out, and_2_out, and_3_out, and_4_out, and_5_out, and_6_out, and_7_out, and_8_out, and_9_out,
       and_10_out, and_11_out, and_12_out, and_13_out, and_14_out, and_15_out, and_16_out, and_17_out,
       and_18_out, and_19_out, and_20_out, and_21_out, and_22_out, and_23_out, and_24_out, nand_1_out,
       nand_2_out, nand_3_out, nand_4_out, nand_5_out, nand_6_out, nand_7_out, nand_8_out, nand_9_out,
       nand_10_out, nand_11_out, nand_12_out, nand_13_out, nand_14_out, nand_15_out, nand_16_out,
       nand_17_out, nand_18_out, nand_19_out, nand_20_out, nand_21_out, nand_22_out, nand_23_out,
       nand_24_out, nand_25_out, nand_26_out, nand_27_out, nand_28_out, nand_29_out, nand_30_out,
       nand_31_out, nand_32_out, nand_33_out, nand_34_out, nand_35_out, nand_36_out, nand_38_out,
       nand_40_out, or_1_out, or_2_out;

  and and_1 (and_1_out, adr1, adr0);
  and and_2 (and_2_out, adr1, ~adr0);  // AND_Gate
  and and_3 (and_3_out, ~adr1, adr0);  // AND_Gate
  and and_4 (and_4_out, ~adr1, ~adr0);  // AND_Gate
  and and_5 (and_5_out, din1, and_1_out);
  and and_6 (and_6_out, din0, and_1_out);
  and and_7 (and_7_out, wr, and_1_out);
  and and_8 (and_8_out, din1, and_2_out);
  and and_9 (and_9_out, din0, and_2_out);
  and and_10 (and_10_out, wr, and_2_out);
  and and_11 (and_11_out, din1, and_3_out);
  and and_12 (and_12_out, din0, and_3_out);
  and and_13 (and_13_out, wr, and_3_out);
  and and_14 (and_14_out, din1, and_4_out);
  and and_15 (and_15_out, din0, and_4_out);
  and and_16 (and_16_out, wr, and_4_out);
  nand nand_1 (nand_1_out, and_5_out, and_7_out);
  nand nand_2 (nand_2_out, nand_1_out, and_7_out);
  nand nand_3 (nand_3_out, and_6_out, and_7_out);
  nand nand_4 (nand_4_out, nand_3_out, and_7_out);
  nand nand_5 (nand_5_out, and_8_out, and_10_out);
  nand nand_6 (nand_6_out, nand_5_out, and_10_out);
  nand nand_7 (nand_7_out, and_9_out, and_10_out);
  nand nand_8 (nand_8_out, nand_7_out, and_10_out);
  nand nand_9 (nand_9_out, and_11_out, and_13_out);
  nand nand_10 (nand_10_out, nand_9_out, and_13_out);
  nand nand_11 (nand_11_out, and_12_out, and_13_out);
  nand nand_12 (nand_12_out, nand_11_out, and_13_out);
  nand nand_13 (nand_13_out, and_14_out, and_16_out);
  nand nand_14 (nand_14_out, nand_13_out, and_16_out);
  nand nand_15 (nand_15_out, and_15_out, and_16_out);
  nand nand_16 (nand_16_out, nand_15_out, and_16_out);
  nand nand_17 (nand_17_out, nand_1_out, nand_18_out);
  nand nand_18 (nand_18_out, nand_17_out, nand_2_out);
  nand nand_19 (nand_19_out, nand_3_out, nand_20_out);
  nand nand_20 (nand_20_out, nand_19_out, nand_4_out);
  nand nand_21 (nand_21_out, nand_5_out, nand_22_out);
  nand nand_22 (nand_22_out, nand_21_out, nand_6_out);
  nand nand_23 (nand_23_out, nand_7_out, nand_24_out);
  nand nand_24 (nand_24_out, nand_23_out, nand_8_out);
  nand nand_25 (nand_25_out, nand_9_out, nand_26_out);
  nand nand_26 (nand_26_out, nand_25_out, nand_10_out);
  nand nand_27 (nand_27_out, nand_11_out, nand_28_out);
  nand nand_28 (nand_28_out, nand_27_out, nand_12_out);
  nand nand_29 (nand_29_out, nand_13_out, nand_30_out);
  nand nand_30 (nand_30_out, nand_29_out, nand_14_out);
  nand nand_31 (nand_31_out, nand_15_out, nand_32_out);
  nand nand_32 (nand_32_out, nand_31_out, nand_16_out);
  and and_17 (and_17_out, nand_17_out, and_1_out);
  and and_18 (and_18_out, nand_19_out, and_1_out);
  and and_19 (and_19_out, nand_21_out, and_2_out);
  and and_20 (and_20_out, nand_23_out, and_2_out);
  and and_21 (and_21_out, nand_25_out, and_3_out);
  and and_22 (and_22_out, nand_27_out, and_3_out);
  and and_23 (and_23_out, nand_29_out, and_4_out);
  and and_24 (and_24_out, nand_31_out, and_4_out);
  or or_1 (or_1_out, and_17_out, and_19_out, and_21_out, and_23_out);
  or or_2 (or_2_out, and_18_out, and_20_out, and_22_out, and_24_out);
  nand nand_33 (nand_33_out, or_1_out, rd);
  nand nand_34 (nand_34_out, nand_33_out, rd);
  nand nand_35 (nand_35_out, or_2_out, rd);
  nand nand_36 (nand_36_out, nand_35_out, rd);
  nand nand_37 (dout1, nand_33_out, nand_38_out);
  nand nand_38 (nand_38_out, dout1, nand_34_out);
  nand nand_39 (dout0, nand_35_out, nand_40_out);
  nand nand_40 (nand_40_out, dout0, nand_36_out);
endmodule
