// Logisim project mem4.circ as structural Verilog: 1 circuit, main circuit main
module main (
  input  in_1,
  input  in_2,
  input  in_3,
  input  in_4,
  input  in_5,
  input  in_6,
  input  in_7,
  input  in_8,
  input  in_9,
  input  in_10,
  input  in_11,
  input  in_12,
  input  in_13,
  input  in_14,
  input  in_15,
  input  in_16,
  input  in_17,
  input  in_18,
  input  in_19,
  input  in_20,
  input  in_21,
  input  in_22,
  input  in_23,
  input  in_24,
  input  in_25,
  input  in_26,
  input  in_27,
  input  in_28,
  input  in_29,
  input  in_30,
  input  in_31,
  input  in_32,
  input  in_33,
  input  in_34,
  input  in_35,
  input  in_36,
  input  in_37,
  input  in_38,
  input  in_39,
  input  in_40,
  input  in_41,
  input  in_42,
  input  in_43,
  input  in_44,
  input  in_45,
  input  in_46,
  input  in_47,
  input  in_48,
  input  in_49,
  input  in_50,
  input  in_51,
  input  in_52,
  input  in_53,
  input  in_54,
  input  in_55,
  input  in_56,
  input  in_57,
  input  in_58,
  input  in_59,
  input  in_60,
  input  in_61,
  input  in_62,
  input  in_63,
  input  in_64,
  input  in_65,
  input  in_66,
  input  in_67,
  input  in_68,
  output out_69,
  output out_70,
  output out_71,
  output out_72
);

  wire and_1_out, and_2_out, and_3_out, and_4_out, and_5_out, and_6_out, and_7_out, and_8_out, and_9_out,
       and_10_out, and_11_out, and_12_out, and_13_out, and_14_out, and_15_out, and_16_out, and_17_out,
       and_18_out, and_19_out, and_20_out, and_21_out, and_22_out, and_23_out, and_24_out, and_25_out,
       and_26_out, and_27_out, and_28_out, and_29_out, and_30_out, and_31_out, and_32_out, and_33_out,
       and_34_out, and_35_out, and_36_out, and_37_out, and_38_out, and_39_out, and_40_out, and_41_out,
       and_42_out, and_43_out, and_44_out, and_45_out, and_46_out, and_47_out, and_48_out, and_49_out,
       and_50_out, and_51_out, and_52_out, and_53_out, and_54_out, and_55_out, and_56_out, and_57_out,
       and_58_out, and_59_out, and_60_out, and_61_out, and_62_out, and_63_out, and_64_out, not_1_out,
       not_2_out, not_3_out, not_4_out, not_5_out, not_6_out, not_7_out, not_8_out, not_9_out, not_10_out,
       not_11_out, not_12_out, not_13_out, not_14_out, not_15_out, not_16_out, not_17_out, not_18_out,
       not_19_out, not_20_out, not_21_out, not_22_out, not_23_out, not_24_out, not_25_out, not_26_out,
       not_27_out, not_28_out, not_29_out, not_30_out, not_31_out, not_32_out, or_1_out, or_2_out, or_3_out,
       or_4_out, or_5_out, or_6_out, or_7_out, or_8_out, or_9_out, or_10_out, or_11_out, or_12_out,
       or_13_out, or_14_out, or_16_out, or_17_out, or_18_out, or_19_out, or_20_out, or_21_out, or_22_out,
       or_23_out, or_24_out, or_25_out, or_26_out, or_27_out, or_28_out, or_29_out, or_30_out, or_31_out,
       or_32_out, or_33_out, or_34_out, or_35_out, or_36_out, or_37_out, or_38_out, or_39_out, or_40_out,
       or_41_out, or_42_out, or_43_out, or_44_out, or_45_out, or_46_out, or_47_out, or_48_out, or_49_out,
       or_50_out, or_51_out, or_52_out, or_53_out, or_54_out, or_55_out, or_56_out, or_57_out;

  not not_1 (not_1_out, in_65);
  not not_2 (not_2_out, in_65);
  not not_3 (not_3_out, in_65);
  not not_4 (not_4_out, in_65);
  not not_5 (not_5_out, in_65);
  not not_6 (not_6_out, in_65);
  not not_7 (not_7_out, in_65);
  not not_8 (not_8_out, in_65);
  not not_9 (not_9_out, in_67);
  not not_10 (not_10_out, in_67);
  not not_11 (not_11_out, in_66);
  not not_12 (not_12_out, in_66);
  not not_13 (not_13_out, in_66);
  not not_14 (not_14_out, in_67);
  not not_15 (not_15_out, in_66);
  not not_16 (not_16_out, in_67);
  not not_17 (not_17_out, in_67);
  not not_18 (not_18_out, in_67);
  not not_19 (not_19_out, in_66);
  not not_20 (not_20_out, in_66);
  not not_21 (not_21_out, in_66);
  not not_22 (not_22_out, in_67);
  not not_23 (not_23_out, in_66);
  not not_24 (not_24_out, in_67);
  not not_25 (not_25_out, in_68);
  not not_26 (not_26_out, in_68);
  not not_27 (not_27_out, in_68);
  not not_28 (not_28_out, in_68);
  not not_29 (not_29_out, in_68);
  not not_30 (not_30_out, in_68);
  not not_31 (not_31_out, in_68);
  not not_32 (not_32_out, in_68);
  and and_1 (and_1_out, in_1, in_65, in_66, in_67, in_68);
  and and_2 (and_2_out, in_2, in_65, in_66, in_67, in_68);
  and and_3 (and_3_out, in_3, in_65, in_66, in_67, in_68);
  and and_4 (and_4_out, in_4, in_65, in_66, in_67, in_68);
  and and_5 (and_5_out, in_5, in_65, in_66, in_67, not_25_out);
  or or_1 (or_1_out, and_5_out, and_1_out);
  and and_6 (and_6_out, in_6, in_65, in_66, in_67, not_25_out);
  and and_7 (and_7_out, in_7, in_65, in_66, in_67, not_25_out);
  and and_8 (and_8_out, in_8, in_65, in_66, in_67, not_25_out);
  and and_9 (and_9_out, in_9, in_65, in_66, not_9_out, in_68);
  or or_2 (or_2_out, and_9_out, or_1_out);
  and and_10 (and_10_out, in_10, in_65, in_66, not_9_out, in_68);
  and and_11 (and_11_out, in_11, in_65, in_66, not_9_out, in_68);
  and and_12 (and_12_out, in_12, in_65, in_66, not_9_out, in_68);
  and and_13 (and_13_out, in_13, in_65, in_66, not_10_out, not_26_out);
  or or_3 (or_3_out, and_13_out, or_2_out);
  and and_14 (and_14_out, in_14, in_65, in_66, not_10_out, not_26_out);
  and and_15 (and_15_out, in_15, in_65, in_66, not_10_out, not_26_out);
  and and_16 (and_16_out, in_16, in_65, in_66, not_10_out, not_26_out);
  and and_17 (and_17_out, in_17, in_65, not_11_out, in_67, in_68);
  or or_4 (or_4_out, and_17_out, or_3_out);
  and and_18 (and_18_out, in_18, in_65, not_11_out, in_67, in_68);
  and and_19 (and_19_out, in_19, in_65, not_11_out, in_67, in_68);
  and and_20 (and_20_out, in_20, in_65, not_11_out, in_67, in_68);
  and and_21 (and_21_out, in_21, in_65, not_12_out, in_67, not_27_out);
  or or_5 (or_5_out, and_21_out, or_4_out);
  and and_22 (and_22_out, in_22, in_65, not_12_out, in_67, not_27_out);
  and and_23 (and_23_out, in_23, in_65, not_12_out, in_67, not_27_out);
  and and_24 (and_24_out, in_24, in_65, not_12_out, in_67, not_27_out);
  and and_25 (and_25_out, in_25, in_65, not_13_out, not_14_out, in_68);
  or or_6 (or_6_out, and_25_out, or_5_out);
  and and_26 (and_26_out, in_26, in_65, not_13_out, not_14_out, in_68);
  and and_27 (and_27_out, in_27, in_65, not_13_out, not_14_out, in_68);
  and and_28 (and_28_out, in_28, in_65, not_13_out, not_14_out, in_68);
  and and_29 (and_29_out, in_29, in_65, not_15_out, not_16_out, not_28_out);
  or or_7 (or_7_out, and_29_out, or_6_out);
  and and_30 (and_30_out, in_30, in_65, not_15_out, not_16_out, not_28_out);
  and and_31 (and_31_out, in_31, in_65, not_15_out, not_16_out, not_28_out);
  and and_32 (and_32_out, in_32, in_65, not_15_out, not_16_out, not_28_out);
  and and_33 (and_33_out, in_33, not_1_out, in_66, in_67, in_68);
  or or_8 (or_8_out, and_33_out, or_7_out);
  and and_34 (and_34_out, in_34, not_1_out, in_66, in_67, in_68);
  and and_35 (and_35_out, in_35, not_1_out, in_66, in_67, in_68);
  and and_36 (and_36_out, in_36, not_1_out, in_66, in_67, in_68);
  and and_37 (and_37_out, in_37, not_2_out, in_66, in_67, not_29_out);
  or or_9 (or_9_out, and_37_out, or_8_out);
  and and_38 (and_38_out, in_38, not_2_out, in_66, in_67, not_29_out);
  and and_39 (and_39_out, in_39, not_2_out, in_66, in_67, not_29_out);
  and and_40 (and_40_out, in_40, not_2_out, in_66, in_67, not_29_out);
  and and_41 (and_41_out, in_41, not_3_out, in_66, not_17_out, in_68);
  or or_10 (or_10_out, and_41_out, or_9_out);
  and and_42 (and_42_out, in_42, not_3_out, in_66, not_17_out, in_68);
  and and_43 (and_43_out, in_43, not_3_out, in_66, not_17_out, in_68);
  and and_44 (and_44_out, in_44, not_3_out, in_66, not_17_out, in_68);
  and and_45 (and_45_out, in_45, not_4_out, in_66, not_18_out, not_30_out);
  or or_11 (or_11_out, and_45_out, or_10_out);
  and and_46 (and_46_out, in_46, not_4_out, in_66, not_18_out, not_30_out);
  and and_47 (and_47_out, in_47, not_4_out, in_66, not_18_out, not_30_out);
  and and_48 (and_48_out, in_48, not_4_out, in_66, not_18_out, not_30_out);
  and and_49 (and_49_out, in_49, not_5_out, not_19_out, in_67, in_68);
  or or_12 (or_12_out, and_49_out, or_11_out);
  and and_50 (and_50_out, in_50, not_5_out, not_19_out, in_67, in_68);
  and and_51 (and_51_out, in_51, not_5_out, not_19_out, in_67, in_68);
  and and_52 (and_52_out, in_52, not_5_out, not_19_out, in_67, in_68);
  and and_53 (and_53_out, in_53, not_6_out, not_20_out, in_67, not_31_out);
  or or_13 (or_13_out, and_53_out, or_12_out);
  and and_54 (and_54_out, in_54, not_6_out, not_20_out, in_67, not_31_out);
  and and_55 (and_55_out, in_55, not_6_out, not_20_out, in_67, not_31_out);
  and and_56 (and_56_out, in_56, not_6_out, not_20_out, in_67, not_31_out);
  and and_57 (and_57_out, in_57, not_7_out, not_21_out, not_22_out, in_68);
  or or_14 (or_14_out, and_57_out, or_13_out);
  and and_58 (and_58_out, in_58, not_7_out, not_21_out, not_22_out, in_68);
  and and_59 (and_59_out, in_59, not_7_out, not_21_out, not_22_out, in_68);
  and and_60 (and_60_out, in_60, not_7_out, not_21_out, not_22_out, in_68);
  and and_61 (and_61_out, in_61, not_8_out, not_23_out, not_24_out, not_32_out);
  or or_15 (out_69, and_61_out, or_14_out);
  and and_62 (and_62_out, in_62, not_8_out, not_23_out, not_24_out, not_32_out);
  and and_63 (and_63_out, in_63, not_8_out, not_23_out, not_24_out, not_32_out);
  and and_64 (and_64_out, in_64, not_8_out, not_23_out, not_24_out, not_32_out);
  or or_16 (or_16_out, and_6_out, and_2_out);
  or or_17 (or_17_out, and_7_out, and_3_out);
  or or_18 (or_18_out, and_8_out, and_4_out);
  or or_19 (or_19_out, and_10_out, or_16_out);
  or or_20 (or_20_out, and_11_out, or_17_out);
  or or_21 (or_21_out, and_12_out, or_18_out);
  or or_22 (or_22_out, and_14_out, or_19_out);
  or or_23 (or_23_out, and_15_out, or_20_out);
  or or_24 (or_24_out, and_16_out, or_21_out);
  or or_25 (or_25_out, and_18_out, or_22_out);
  or or_26 (or_26_out, and_19_out, or_23_out);
  or or_27 (or_27_out, and_20_out, or_24_out);
  or or_28 (or_28_out, and_22_out, or_25_out);
  or or_29 (or_29_out, and_23_out, or_26_out);
  or or_30 (or_30_out, and_24_out, or_27_out);
  or or_31 (or_31_out, and_26_out, or_28_out);
  or or_32 (or_32_out, and_27_out, or_29_out);
  or or_33 (or_33_out, and_28_out, or_30_out);
  or or_34 (or_34_out, and_30_out, or_31_out);
  or or_35 (or_35_out, and_31_out, or_32_out);
  or or_36 (or_36_out, and_32_out, or_33_out);
  or or_37 (or_37_out, and_34_out, or_34_out);
  or or_38 (or_38_out, and_35_out, or_35_out);
  or or_39 (or_39_out, and_36_out, or_36_out);
  or or_40 (or_40_out, and_38_out, or_37_out);
  or or_41 (or_41_out, and_39_out, or_38_out);
  or or_42 (or_42_out, and_40_out, or_39_out);
  or or_43 (or_43_out, and_42_out, or_40_out);
  or or_44 (or_44_out, and_43_out, or_41_out);
  or or_45 (or_45_out, and_44_out, or_42_out);
  or or_46 (or_46_out, and_46_out, or_43_out);
  or or_47 (or_47_out, and_47_out, or_44_out);
  or or_48 (or_48_out, and_48_out, or_45_out);
  or or_49 (or_49_out, and_50_out, or_46_out);
  or or_50 (or_50_out, and_51_out, or_47_out);
  or or_51 (or_51_out, and_52_out, or_48_out);
  or or_52 (or_52_out, and_54_out, or_49_out);
  or or_53 (or_53_out, and_55_out, or_50_out);
  or or_54 (or_54_out, and_56_out, or_51_out);
  or or_55 (or_55_out, and_58_out, or_52_out);
  or or_56 (or_56_out, and_59_out, or_53_out);
  or or_57 (or_57_out, and_60_out, or_54_out);
  or or_58 (out_70, and_62_out, or_55_out);
  or or_59 (out_71, and_63_out, or_56_out);
  or or_60 (out_72, and_64_out, or_57_out);
endmodule
