// Logisim project seqA.circ as structural Verilog: 1 circuit, main circuit main
module main (
  input  [7:0] instruction,
  output [7:0] address,
  output [1:0] op0,
  output [1:0] op1
);

  wire clock_1_out;
  wire [7:0] counter_1_q, rom_1_data;

  Clock clock_1 (.out(clock_1_out));
  ROM #(.addrWidth(4)) rom_1 (.addr(instruction[7:4]), .data(rom_1_data));  // open: sel
  Counter counter_1 (.D(rom_1_data), .Q(counter_1_q), .clk(clock_1_out));  // open: load, count, carry, clr
  ROM rom_2 (.addr(counter_1_q));  // open: data, sel
  Counter PC (.Q(address));  // open: load, D, count, carry, clk, clr
endmodule
