// Logisim project seqtest.circ as structural Verilog: 1 circuit, main circuit main
module main (
  input  in_1,
  input  in_2,
  input  in_3,
  input  in_4
);

  wire clock_1_out;
  wire [3:0] counter_1_q;
  wire [7:0] rom_1_data;

  Clock clock_1 (.out(clock_1_out));
  Counter #(.width(4), .max('hf)) counter_1 (
    .load(1'b0), .count(1'b1), .Q(counter_1_q), .clk(clock_1_out));  // open: D, carry, clr
  ROM rom_1 (.addr({in_1, in_2, in_3, in_4, counter_1_q}), .data(rom_1_data));  // open: sel
  DotMatrix #(.inputtype("row"), .matrixcols(8), .matrixrows(1)) dotmatrix_1 (.row0(rom_1_data));

  // Notes on the sheet:
  //   contents of rom_1 (hex, n*v repeats v):
  //   1 2 4 8 10 20 40 80 1 2 4 8 10 20 40 80 80 40 20 10 8 4 2 1 80 40 20 10 8 4 2 1 8*0 4*2 0 4 0 4 8*0
  //   4*1 0 8 0 8 8*0 4*8 0 10 0 10 8*0 4*4 0 20 0 20 8*0 4*2 0 40 0 40 8*0 4*1 0 80 0 80 8*0 4*8 1 0 1
  //   9*0 4*4 2 0 2 9*0 4*2 4 0 4 9*0 4*1 8 0 8 9*0 4*8 10 0 10 9*0 4*4 20 0 20 9*0 4*2 40 0 40 9*0 4*1 80
  //   0 80
endmodule
